// Logisim project ROM16x8.circ as structural Verilog: 1 circuit, main circuit main
module main (
  input  in_1,
  input  in_2,
  input  in_3,
  input  in_4,
  input  in_5,
  input  in_6,
  input  in_7,
  input  in_8,
  input  in_9,
  input  in_10,
  input  in_11,
  input  in_12,
  input  in_13,
  input  in_14,
  input  in_15,
  input  in_16,
  input  in_17,
  input  in_18,
  input  in_19,
  input  in_20,
  input  in_21,
  input  in_22,
  input  in_23,
  input  in_24,
  input  in_25,
  input  in_26,
  input  in_27,
  input  in_28,
  input  in_29,
  input  in_30,
  input  in_31,
  input  in_32,
  input  in_33,
  input  in_34,
  input  in_35,
  input  in_36,
  input  in_37,
  input  in_38,
  input  in_39,
  input  in_40,
  input  in_41,
  input  in_42,
  input  in_43,
  input  in_44,
  input  in_45,
  input  in_46,
  input  in_47,
  input  in_48,
  input  in_49,
  input  in_50,
  input  in_51,
  input  in_52,
  input  in_53,
  input  in_54,
  input  in_55,
  input  in_56,
  input  in_57,
  input  in_58,
  input  in_59,
  input  in_60,
  input  in_61,
  input  in_62,
  input  in_63,
  input  in_64,
  input  in_65,
  input  in_66,
  input  in_67,
  input  in_68,
  input  in_69,
  input  in_70,
  input  in_71,
  input  in_72,
  input  EN,
  input  [3:0] addr,
  input  in_75,
  input  in_76,
  input  in_77,
  input  in_78,
  input  in_79,
  input  in_80,
  input  in_81,
  input  in_82,
  input  in_83,
  input  in_84,
  input  in_85,
  input  in_86,
  input  in_87,
  input  in_88,
  input  in_89,
  input  in_90,
  input  in_91,
  input  in_92,
  input  in_93,
  input  in_94,
  input  in_95,
  input  in_96,
  input  in_97,
  input  in_98,
  input  in_99,
  input  in_100,
  input  in_101,
  input  in_102,
  input  in_103,
  input  in_104,
  input  in_105,
  input  in_106,
  input  in_107,
  input  in_108,
  input  in_109,
  input  in_110,
  input  in_111,
  input  in_112,
  input  in_113,
  input  in_114,
  input  in_115,
  input  in_116,
  input  in_117,
  input  in_118,
  input  in_119,
  input  in_120,
  input  in_121,
  input  in_122,
  input  in_123,
  input  in_124,
  input  in_125,
  input  in_126,
  input  in_127,
  input  in_128,
  input  in_129,
  input  in_130,
  output [7:0] D
);

  wire and_1_out, and_2_out, and_3_out, and_4_out, and_5_out, and_6_out, and_7_out, and_8_out, and_9_out,
       and_10_out, and_11_out, and_12_out, and_13_out, and_14_out, and_15_out, and_16_out, and_17_out,
       and_18_out, and_19_out, and_20_out, and_21_out, and_22_out, and_23_out, and_24_out, and_25_out,
       and_26_out, and_27_out, and_28_out, and_29_out, and_30_out, and_31_out, and_32_out, and_33_out,
       and_34_out, and_35_out, and_36_out, and_37_out, and_38_out, and_39_out, and_40_out, and_41_out,
       and_42_out, and_43_out, and_44_out, and_45_out, and_46_out, and_47_out, and_48_out, and_49_out,
       and_50_out, and_51_out, and_52_out, and_53_out, and_54_out, and_55_out, and_56_out, and_57_out,
       and_58_out, and_59_out, and_60_out, and_61_out, and_62_out, and_63_out, and_64_out, and_65_out,
       and_66_out, and_67_out, and_68_out, and_69_out, and_70_out, and_71_out, and_72_out, and_73_out,
       and_74_out, and_75_out, and_76_out, and_77_out, and_78_out, and_79_out, and_80_out, and_81_out,
       and_82_out, and_83_out, and_84_out, and_85_out, and_86_out, and_87_out, and_88_out, and_89_out,
       and_90_out, and_91_out, and_92_out, and_93_out, and_94_out, and_95_out, and_96_out, and_97_out,
       and_98_out, and_99_out, and_100_out, and_101_out, and_102_out, and_103_out, and_104_out, and_105_out,
       and_106_out, and_107_out, and_108_out, and_109_out, and_110_out, and_111_out, and_112_out,
       and_113_out, and_114_out, and_115_out, and_116_out, and_117_out, and_118_out, and_119_out,
       and_120_out, and_121_out, and_122_out, and_123_out, and_124_out, and_125_out, and_126_out,
       and_127_out, and_128_out, decoder_1_out0, decoder_1_out1, decoder_1_out2, decoder_1_out3,
       decoder_1_out4, decoder_1_out5, decoder_1_out6, decoder_1_out7, decoder_1_out8, decoder_1_out9,
       decoder_1_out10, decoder_1_out11, decoder_1_out12, decoder_1_out13, decoder_1_out14, decoder_1_out15;

  Decoder #(.select(4)) decoder_1 (
    .out0(decoder_1_out0), .out1(decoder_1_out1), .out2(decoder_1_out2), .out3(decoder_1_out3),
    .out4(decoder_1_out4), .out5(decoder_1_out5), .out6(decoder_1_out6), .out7(decoder_1_out7),
    .out8(decoder_1_out8), .out9(decoder_1_out9), .out10(decoder_1_out10), .out11(decoder_1_out11),
    .out12(decoder_1_out12), .out13(decoder_1_out13), .out14(decoder_1_out14), .out15(decoder_1_out15),
    .sel(addr), .en(EN));
  and and_1 (and_1_out, decoder_1_out0, in_1);
  and and_2 (and_2_out, decoder_1_out1, in_9);
  and and_3 (and_3_out, decoder_1_out2, in_17);
  and and_4 (and_4_out, decoder_1_out3, in_25);
  and and_5 (and_5_out, decoder_1_out4, in_33);
  and and_6 (and_6_out, decoder_1_out5, in_41);
  and and_7 (and_7_out, decoder_1_out6, in_49);
  and and_8 (and_8_out, decoder_1_out7, in_57);
  and and_9 (and_9_out, decoder_1_out8, in_65);
  and and_10 (and_10_out, decoder_1_out9, in_75);
  and and_11 (and_11_out, decoder_1_out10, in_83);
  and and_12 (and_12_out, decoder_1_out11, in_91);
  and and_13 (and_13_out, decoder_1_out12, in_99);
  and and_14 (and_14_out, decoder_1_out13, in_107);
  and and_15 (and_15_out, decoder_1_out14, in_115);
  and and_16 (and_16_out, decoder_1_out15, in_123);
  or D7 (D[7], and_16_out, and_15_out, and_14_out, and_13_out, and_12_out, and_11_out, and_10_out, and_9_out, and_8_out, and_7_out, and_6_out, and_5_out, and_4_out, and_3_out, and_2_out, and_1_out);
  and and_17 (and_17_out, decoder_1_out0, in_2);
  and and_18 (and_18_out, decoder_1_out1, in_10);
  and and_19 (and_19_out, decoder_1_out2, in_18);
  and and_20 (and_20_out, decoder_1_out3, in_26);
  and and_21 (and_21_out, decoder_1_out4, in_34);
  and and_22 (and_22_out, decoder_1_out5, in_42);
  and and_23 (and_23_out, decoder_1_out6, in_50);
  and and_24 (and_24_out, decoder_1_out7, in_58);
  and and_25 (and_25_out, decoder_1_out8, in_66);
  and and_26 (and_26_out, decoder_1_out9, in_76);
  and and_27 (and_27_out, decoder_1_out10, in_84);
  and and_28 (and_28_out, decoder_1_out11, in_92);
  and and_29 (and_29_out, decoder_1_out12, in_100);
  and and_30 (and_30_out, decoder_1_out13, in_108);
  and and_31 (and_31_out, decoder_1_out14, in_116);
  and and_32 (and_32_out, decoder_1_out15, in_124);
  or D6 (D[6], and_32_out, and_31_out, and_30_out, and_29_out, and_28_out, and_27_out, and_26_out, and_25_out, and_24_out, and_23_out, and_22_out, and_21_out, and_20_out, and_19_out, and_18_out, and_17_out);
  and and_33 (and_33_out, decoder_1_out0, in_3);
  and and_34 (and_34_out, decoder_1_out1, in_11);
  and and_35 (and_35_out, decoder_1_out2, in_19);
  and and_36 (and_36_out, decoder_1_out3, in_27);
  and and_37 (and_37_out, decoder_1_out4, in_35);
  and and_38 (and_38_out, decoder_1_out5, in_43);
  and and_39 (and_39_out, decoder_1_out6, in_51);
  and and_40 (and_40_out, decoder_1_out7, in_59);
  and and_41 (and_41_out, decoder_1_out8, in_67);
  and and_42 (and_42_out, decoder_1_out9, in_77);
  and and_43 (and_43_out, decoder_1_out10, in_85);
  and and_44 (and_44_out, decoder_1_out11, in_93);
  and and_45 (and_45_out, decoder_1_out12, in_101);
  and and_46 (and_46_out, decoder_1_out13, in_109);
  and and_47 (and_47_out, decoder_1_out14, in_117);
  and and_48 (and_48_out, decoder_1_out15, in_125);
  or D5 (D[5], and_48_out, and_47_out, and_46_out, and_45_out, and_44_out, and_43_out, and_42_out, and_41_out, and_40_out, and_39_out, and_38_out, and_37_out, and_36_out, and_35_out, and_34_out, and_33_out);
  and and_49 (and_49_out, decoder_1_out0, in_4);
  and and_50 (and_50_out, decoder_1_out1, in_12);
  and and_51 (and_51_out, decoder_1_out2, in_20);
  and and_52 (and_52_out, decoder_1_out3, in_28);
  and and_53 (and_53_out, decoder_1_out4, in_36);
  and and_54 (and_54_out, decoder_1_out5, in_44);
  and and_55 (and_55_out, decoder_1_out6, in_52);
  and and_56 (and_56_out, decoder_1_out7, in_60);
  and and_57 (and_57_out, decoder_1_out8, in_68);
  and and_58 (and_58_out, decoder_1_out9, in_78);
  and and_59 (and_59_out, decoder_1_out10, in_86);
  and and_60 (and_60_out, decoder_1_out11, in_94);
  and and_61 (and_61_out, decoder_1_out12, in_102);
  and and_62 (and_62_out, decoder_1_out13, in_110);
  and and_63 (and_63_out, decoder_1_out14, in_118);
  and and_64 (and_64_out, decoder_1_out15, in_126);
  or D4 (D[4], and_64_out, and_63_out, and_62_out, and_61_out, and_60_out, and_59_out, and_58_out, and_57_out, and_56_out, and_55_out, and_54_out, and_53_out, and_52_out, and_51_out, and_50_out, and_49_out);
  and and_65 (and_65_out, decoder_1_out0, in_5);
  and and_66 (and_66_out, decoder_1_out1, in_13);
  and and_67 (and_67_out, decoder_1_out2, in_21);
  and and_68 (and_68_out, decoder_1_out3, in_29);
  and and_69 (and_69_out, decoder_1_out4, in_37);
  and and_70 (and_70_out, decoder_1_out5, in_45);
  and and_71 (and_71_out, decoder_1_out6, in_53);
  and and_72 (and_72_out, decoder_1_out7, in_61);
  and and_73 (and_73_out, decoder_1_out8, in_69);
  and and_74 (and_74_out, decoder_1_out9, in_79);
  and and_75 (and_75_out, decoder_1_out10, in_87);
  and and_76 (and_76_out, decoder_1_out11, in_95);
  and and_77 (and_77_out, decoder_1_out12, in_103);
  and and_78 (and_78_out, decoder_1_out13, in_111);
  and and_79 (and_79_out, decoder_1_out14, in_119);
  and and_80 (and_80_out, decoder_1_out15, in_127);
  or D3 (D[3], and_80_out, and_79_out, and_78_out, and_77_out, and_76_out, and_75_out, and_74_out, and_73_out, and_72_out, and_71_out, and_70_out, and_69_out, and_68_out, and_67_out, and_66_out, and_65_out);
  and and_81 (and_81_out, decoder_1_out0, in_6);
  and and_82 (and_82_out, decoder_1_out1, in_14);
  and and_83 (and_83_out, decoder_1_out2, in_22);
  and and_84 (and_84_out, decoder_1_out3, in_30);
  and and_85 (and_85_out, decoder_1_out4, in_38);
  and and_86 (and_86_out, decoder_1_out5, in_46);
  and and_87 (and_87_out, decoder_1_out6, in_54);
  and and_88 (and_88_out, decoder_1_out7, in_62);
  and and_89 (and_89_out, decoder_1_out8, in_70);
  and and_90 (and_90_out, decoder_1_out9, in_80);
  and and_91 (and_91_out, decoder_1_out10, in_88);
  and and_92 (and_92_out, decoder_1_out11, in_96);
  and and_93 (and_93_out, decoder_1_out12, in_104);
  and and_94 (and_94_out, decoder_1_out13, in_112);
  and and_95 (and_95_out, decoder_1_out14, in_120);
  and and_96 (and_96_out, decoder_1_out15, in_128);
  or D2 (D[2], and_96_out, and_95_out, and_94_out, and_93_out, and_92_out, and_91_out, and_90_out, and_89_out, and_88_out, and_87_out, and_86_out, and_85_out, and_84_out, and_83_out, and_82_out, and_81_out);
  and and_97 (and_97_out, decoder_1_out0, in_7);
  and and_98 (and_98_out, decoder_1_out1, in_15);
  and and_99 (and_99_out, decoder_1_out2, in_23);
  and and_100 (and_100_out, decoder_1_out3, in_31);
  and and_101 (and_101_out, decoder_1_out4, in_39);
  and and_102 (and_102_out, decoder_1_out5, in_47);
  and and_103 (and_103_out, decoder_1_out6, in_55);
  and and_104 (and_104_out, decoder_1_out7, in_63);
  and and_105 (and_105_out, decoder_1_out8, in_71);
  and and_106 (and_106_out, decoder_1_out9, in_81);
  and and_107 (and_107_out, decoder_1_out10, in_89);
  and and_108 (and_108_out, decoder_1_out11, in_97);
  and and_109 (and_109_out, decoder_1_out12, in_105);
  and and_110 (and_110_out, decoder_1_out13, in_113);
  and and_111 (and_111_out, decoder_1_out14, in_121);
  and and_112 (and_112_out, decoder_1_out15, in_129);
  or D1 (D[1], and_112_out, and_111_out, and_110_out, and_109_out, and_108_out, and_107_out, and_106_out, and_105_out, and_104_out, and_103_out, and_102_out, and_101_out, and_100_out, and_99_out, and_98_out, and_97_out);
  and and_113 (and_113_out, decoder_1_out0, in_8);
  and and_114 (and_114_out, decoder_1_out1, in_16);
  and and_115 (and_115_out, decoder_1_out2, in_24);
  and and_116 (and_116_out, decoder_1_out3, in_32);
  and and_117 (and_117_out, decoder_1_out4, in_40);
  and and_118 (and_118_out, decoder_1_out5, in_48);
  and and_119 (and_119_out, decoder_1_out6, in_56);
  and and_120 (and_120_out, decoder_1_out7, in_64);
  and and_121 (and_121_out, decoder_1_out8, in_72);
  and and_122 (and_122_out, decoder_1_out9, in_82);
  and and_123 (and_123_out, decoder_1_out10, in_90);
  and and_124 (and_124_out, decoder_1_out11, in_98);
  and and_125 (and_125_out, decoder_1_out12, in_106);
  and and_126 (and_126_out, decoder_1_out13, in_114);
  and and_127 (and_127_out, decoder_1_out14, in_122);
  and and_128 (and_128_out, decoder_1_out15, in_130);
  or D0 (D[0], and_128_out, and_127_out, and_126_out, and_125_out, and_124_out, and_123_out, and_122_out, and_121_out, and_120_out, and_119_out, and_118_out, and_117_out, and_116_out, and_115_out, and_114_out, and_113_out);
endmodule
