// Logisim project num_repr_compute.circ as structural Verilog
module fa1bit (
  input  A,
  input  B,
  input  Cin,
  output S,
  output Cout
);

  wire and_1_out, and_2_out, and_3_out;

  and and_1 (and_1_out, A, B);
  and and_2 (and_2_out, B, Cin);
  and and_3 (and_3_out, A, Cin);
  xor xor_1 (S, A, B, Cin);
  or or_1 (Cout, and_1_out, and_2_out, and_3_out);
endmodule

module fs1bit (
  input  A,
  input  B,
  input  Bin,
  output D,
  output Bout
);

  wire and_1_out, and_2_out, and_3_out, not_1_out;

  not not_1 (not_1_out, A);
  and and_1 (and_1_out, not_1_out, B);
  and and_2 (and_2_out, not_1_out, Bin);
  and and_3 (and_3_out, B, Bin);
  xor xor_1 (D, A, B, Bin);
  or or_1 (Bout, and_1_out, and_2_out, and_3_out);
endmodule

module decoder_1_2 (
  input  A0,
  output Y0,
  output Y1
);

  not not_1 (Y0, A0);

  assign Y1 = A0;
endmodule

module mux_3_2_1 (
  input  S0,
  input  D00,
  input  D01,
  input  D10,
  input  D11,
  input  D20,
  input  D21,
  output Y0,
  output Y1,
  output Y2
);

  wire and_1_out, and_2_out, and_3_out, and_4_out, and_5_out, and_6_out, decoder_1_2_1_y0, decoder_1_2_1_y1;

  decoder_1_2 decoder_1_2_1 (.A0(S0), .Y0(decoder_1_2_1_y0), .Y1(decoder_1_2_1_y1));
  and and_1 (and_1_out, D00, decoder_1_2_1_y0);
  and and_2 (and_2_out, D01, decoder_1_2_1_y1);
  and and_3 (and_3_out, D10, decoder_1_2_1_y0);
  and and_4 (and_4_out, D11, decoder_1_2_1_y1);
  and and_5 (and_5_out, D20, decoder_1_2_1_y0);
  and and_6 (and_6_out, D21, decoder_1_2_1_y1);
  or or_1 (Y0, and_1_out, and_2_out);
  or or_2 (Y1, and_3_out, and_4_out);
  or or_3 (Y2, and_5_out, and_6_out);
endmodule

module mux_2_1 (
  input  S,
  input  D0,
  input  D1,
  output out_4
);

  wire and_1_out, and_2_out, decoder_1_2_1_y0, decoder_1_2_1_y1;

  decoder_1_2 decoder_1_2_1 (.A0(S), .Y0(decoder_1_2_1_y0), .Y1(decoder_1_2_1_y1));
  and and_1 (and_1_out, D0, decoder_1_2_1_y0);
  and and_2 (and_2_out, decoder_1_2_1_y1, D1);
  or or_1 (out_4, and_1_out, and_2_out);
endmodule

module samadder4bit (
  input  [3:0] A,
  input  [3:0] B,
  output [3:0] Y
);

  wire and_1_out, fa1bit_1_cout, fa1bit_1_s, fa1bit_2_cout, fa1bit_2_s, fa1bit_3_cout, fa1bit_3_s,
       fs1bit_1_bout, fs1bit_1_d, fs1bit_2_bout, fs1bit_2_d, fs1bit_3_bout, fs1bit_3_d, fs1bit_4_bout,
       fs1bit_4_d, fs1bit_5_bout, fs1bit_5_d, fs1bit_6_d, mux_3_2_1_1_y0, mux_3_2_1_1_y1, mux_3_2_1_1_y2,
       not_1_out, xor_1_out;

  xor xor_1 (xor_1_out, A[3], B[3]);
  fa1bit fa1bit_1 (.A(A[0]), .B(B[0]), .S(fa1bit_1_s), .Cout(fa1bit_1_cout));  // open: Cin
  fa1bit fa1bit_2 (.A(A[1]), .B(B[1]), .Cin(fa1bit_1_cout), .S(fa1bit_2_s), .Cout(fa1bit_2_cout));
  fa1bit fa1bit_3 (.A(A[2]), .B(B[2]), .Cin(fa1bit_2_cout), .S(fa1bit_3_s), .Cout(fa1bit_3_cout));
  fs1bit fs1bit_1 (.A(A[0]), .B(B[0]), .D(fs1bit_1_d), .Bout(fs1bit_1_bout));  // open: Bin
  fs1bit fs1bit_2 (.A(A[1]), .B(B[1]), .Bin(fs1bit_1_bout), .D(fs1bit_2_d), .Bout(fs1bit_2_bout));
  fs1bit fs1bit_3 (.A(A[2]), .B(B[2]), .Bin(fs1bit_2_bout), .D(fs1bit_3_d), .Bout(fs1bit_3_bout));
  fs1bit fs1bit_4 (.A(B[0]), .B(A[0]), .D(fs1bit_4_d), .Bout(fs1bit_4_bout));  // open: Bin
  fs1bit fs1bit_5 (.A(B[1]), .B(A[1]), .Bin(fs1bit_4_bout), .D(fs1bit_5_d), .Bout(fs1bit_5_bout));
  fs1bit fs1bit_6 (.A(B[2]), .B(A[2]), .Bin(fs1bit_5_bout), .D(fs1bit_6_d));  // open: Bout
  not not_1 (not_1_out, xor_1_out);
  mux_3_2_1 mux_3_2_1_1 (
    .S0(fs1bit_3_bout), .D00(fs1bit_1_d), .D01(fs1bit_4_d), .D10(fs1bit_2_d), .D11(fs1bit_5_d),
    .D20(fs1bit_3_d), .D21(fs1bit_6_d), .Y0(mux_3_2_1_1_y0), .Y1(mux_3_2_1_1_y1), .Y2(mux_3_2_1_1_y2));
  mux_2_1 mux_2_1_1 (.S(fs1bit_3_bout), .D0(A[3]), .D1(B[3]), .out_4(Y[3]));
  and and_1 (and_1_out, fa1bit_3_cout, not_1_out);
  mux_3_2_1 mux_3_2_1_2 (
    .S0(xor_1_out), .D00(fa1bit_1_s), .D01(mux_3_2_1_1_y0), .D10(fa1bit_2_s), .D11(mux_3_2_1_1_y1),
    .D20(fa1bit_3_s), .D21(mux_3_2_1_1_y2), .Y0(Y[0]), .Y1(Y[1]), .Y2(Y[2]));
  LED led_1 (.in(and_1_out));
endmodule

module com1adder4bit (
  input  [3:0] A,
  input  [3:0] B,
  output [3:0] out_3
);

  wire not_1_out, not_2_out, not_3_out, not_4_out, not_5_out, not_6_out;
  wire [2:0] mux_3_2_1_1_y0, mux_3_2_1_2_y0;

  not not_1 (not_1_out, A[0]);
  not not_2 (not_2_out, A[1]);
  not not_3 (not_3_out, A[2]);
  not not_4 (not_4_out, B[0]);
  not not_5 (not_5_out, B[1]);
  not not_6 (not_6_out, B[2]);
  mux_3_2_1 mux_3_2_1_1 (
    .S0(A[3]), .D00(A[0]), .D01(not_1_out), .D10(A[1]), .D11(not_2_out), .D20(A[2]), .D21(not_3_out),
    .Y0(mux_3_2_1_1_y0[0]), .Y1(mux_3_2_1_1_y0[1]), .Y2(mux_3_2_1_1_y0[2]));
  mux_3_2_1 mux_3_2_1_2 (
    .S0(B[3]), .D00(B[0]), .D01(not_4_out), .D10(B[1]), .D11(not_5_out), .D20(B[2]), .D21(not_6_out),
    .Y0(mux_3_2_1_2_y0[0]), .Y1(mux_3_2_1_2_y0[1]), .Y2(mux_3_2_1_2_y0[2]));
  samadder4bit samadder4bit_1 (.A({A[3], mux_3_2_1_1_y0}), .B({B[3], mux_3_2_1_2_y0}), .Y(out_3));
endmodule

module mux_4_2_1 (
  input  S0,
  input  D00,
  input  D01,
  input  D10,
  input  D11,
  input  D20,
  input  D21,
  input  D30,
  input  D31,
  output Y0,
  output Y1,
  output Y2,
  output Y3
);

  wire and_1_out, and_2_out, and_3_out, and_4_out, and_5_out, and_6_out, and_7_out, and_8_out,
       decoder_1_2_1_y0, decoder_1_2_1_y1;

  decoder_1_2 decoder_1_2_1 (.A0(S0), .Y0(decoder_1_2_1_y0), .Y1(decoder_1_2_1_y1));
  and and_1 (and_1_out, D00, decoder_1_2_1_y0);
  and and_2 (and_2_out, D01, decoder_1_2_1_y1);
  and and_3 (and_3_out, D10, decoder_1_2_1_y0);
  and and_4 (and_4_out, D11, decoder_1_2_1_y1);
  and and_5 (and_5_out, D20, decoder_1_2_1_y0);
  and and_6 (and_6_out, D21, decoder_1_2_1_y1);
  and and_7 (and_7_out, D30, decoder_1_2_1_y0);
  and and_8 (and_8_out, D31, decoder_1_2_1_y1);
  or or_1 (Y0, and_1_out, and_2_out);
  or or_2 (Y1, and_3_out, and_4_out);
  or or_3 (Y2, and_5_out, and_6_out);
  or or_4 (Y3, and_7_out, and_8_out);
endmodule

module com1adder4bit_based_rca (
  input  [3:0] A,
  input  [3:0] B,
  output [3:0] out_3
);

  wire fa1bit_1_cout, fa1bit_2_cout, fa1bit_3_cout, fa1bit_4_cout;

  fa1bit fa1bit_1 (.A(A[0]), .B(B[0]), .Cin(fa1bit_4_cout), .S(out_3[0]), .Cout(fa1bit_1_cout));
  fa1bit fa1bit_2 (.A(A[1]), .B(B[1]), .Cin(fa1bit_1_cout), .S(out_3[1]), .Cout(fa1bit_2_cout));
  fa1bit fa1bit_3 (.A(A[2]), .B(B[2]), .Cin(fa1bit_2_cout), .S(out_3[2]), .Cout(fa1bit_3_cout));
  fa1bit fa1bit_4 (.A(A[3]), .B(B[3]), .Cin(fa1bit_3_cout), .S(out_3[3]), .Cout(fa1bit_4_cout));
endmodule

module com2adder4bit (
  input  [3:0] A,
  input  Sub,
  input  [3:0] B,
  output [3:0] Y,
  output Cout
);

  wire fa1bit_1_cout, fa1bit_2_cout, fa1bit_3_cout, mux_4_2_1_1_y0, mux_4_2_1_1_y1, mux_4_2_1_1_y2,
       mux_4_2_1_1_y3, not_1_out, not_2_out, not_3_out, not_4_out, xor_1_out;

  not not_1 (not_1_out, B[0]);
  not not_2 (not_2_out, B[1]);
  not not_3 (not_3_out, B[2]);
  not not_4 (not_4_out, B[3]);
  mux_4_2_1 mux_4_2_1_1 (
    .S0(Sub), .D00(B[0]), .D01(not_1_out), .D10(B[1]), .D11(not_2_out), .D20(B[2]), .D21(not_3_out),
    .D30(B[3]), .D31(not_4_out), .Y0(mux_4_2_1_1_y0), .Y1(mux_4_2_1_1_y1), .Y2(mux_4_2_1_1_y2),
    .Y3(mux_4_2_1_1_y3));
  fa1bit fa1bit_1 (.A(A[0]), .B(mux_4_2_1_1_y0), .Cin(Sub), .S(Y[0]), .Cout(fa1bit_1_cout));
  fa1bit fa1bit_2 (.A(A[1]), .B(mux_4_2_1_1_y1), .Cin(fa1bit_1_cout), .S(Y[1]), .Cout(fa1bit_2_cout));
  fa1bit fa1bit_3 (.A(A[2]), .B(mux_4_2_1_1_y2), .Cin(fa1bit_2_cout), .S(Y[2]), .Cout(fa1bit_3_cout));
  fa1bit fa1bit_4 (.A(A[3]), .B(mux_4_2_1_1_y3), .Cin(fa1bit_3_cout), .S(Y[3]), .Cout(Cout));
  xor xor_1 (xor_1_out, Cout, fa1bit_3_cout);
  LED led_1 (.in(xor_1_out));
endmodule
