// Logisim project sCPU.circ as structural Verilog: 7 circuits, main circuit main
module main (
  input  in_1,
  input  in_2,
  output [7:0] Instruction
);

  wire and_1_out, clock_1_out, comparator_1_eq, decoder_1_out0, decoder_1_out1, decoder_1_out2,
       decoder_1_out3, hex7seg_1_a, hex7seg_1_b, hex7seg_1_c, hex7seg_1_d, hex7seg_1_e, hex7seg_1_f,
       hex7seg_1_g, hex7seg_1_p, not_1_out, or_1_out;
  wire [1:0] multiplexer_3_out;
  wire [3:0] adder_1_out, multiplexer_2_out, pc_1_q;
  wire [7:0] adder_2_out, gprs_1_q0, gprs_1_q1, multiplexer_1_out;

  Clock clock_1 (.out(clock_1_out));
  Multiplexer #(.width(8)) multiplexer_1 (
    .in0({4'b0000, Instruction[3:0]}), .in1(adder_2_out), .out(multiplexer_1_out), .sel(decoder_1_out0));
  Multiplexer #(.width(4)) multiplexer_2 (
    .in0(adder_1_out), .in1(Instruction[5:2]), .out(multiplexer_2_out), .sel(and_1_out));
  or or_1 (or_1_out, decoder_1_out2, decoder_1_out0);
  Multiplexer #(.width(2)) multiplexer_3 (
    .in0(Instruction[3:2]), .in1(2'b00), .out(multiplexer_3_out), .sel(decoder_1_out3));
  Adder #(.width(4)) adder_1 (.a(pc_1_q), .b(4'b0001), .out(adder_1_out));  // open: cin, cout
  ROM #(.addrWidth(4)) rom_1 (.addr(pc_1_q), .data(Instruction));
  PC pc_1 (.RST(in_1), .clk(clock_1_out), .WE(in_2), .D(multiplexer_2_out), .Q(pc_1_q));
  GPRs gprs_1 (
    .RST(in_1), .wdata(multiplexer_1_out), .clk(clock_1_out), .WE(or_1_out), .waddr(Instruction[5:4]),
    .raddr0(multiplexer_3_out), .raddr1(Instruction[1:0]), .Q1(gprs_1_q1), .Q0(gprs_1_q0));
  Adder adder_2 (.a(gprs_1_q1), .b(gprs_1_q0), .out(adder_2_out));  // open: cin, cout
  not not_1 (not_1_out, comparator_1_eq);
  Comparator comparator_1 (.a(gprs_1_q1), .b(gprs_1_q0), .eq(comparator_1_eq));  // open: gt, lt
  and and_1 (and_1_out, not_1_out, decoder_1_out3);
  Decoder #(.select(2)) decoder_1 (
    .out0(decoder_1_out0), .out1(decoder_1_out1), .out2(decoder_1_out2), .out3(decoder_1_out3),
    .sel(Instruction[7:6]), .en(1'b1));
  hex7seg hex7seg_1 (
    .D3(gprs_1_q1[3]), .D2(gprs_1_q1[2]), .D1(gprs_1_q1[1]), .D0(gprs_1_q1[0]), .EN(decoder_1_out1),
    .A(hex7seg_1_a), .B(hex7seg_1_b), .C(hex7seg_1_c), .D(hex7seg_1_d), .E(hex7seg_1_e), .F(hex7seg_1_f),
    .G(hex7seg_1_g), .P(hex7seg_1_p));  // open: Point
  _7_Segment_Display u_7_segment_display_1 (
    .g(hex7seg_1_g), .f(hex7seg_1_f), .a(hex7seg_1_a), .b(hex7seg_1_b), .e(hex7seg_1_e), .d(hex7seg_1_d),
    .c(hex7seg_1_c), .dp(hex7seg_1_p));
  // also tied to GND on the sheet: gprs_1_q1[7:4]

  // Notes on the sheet:
  //   contents of rom_1 (hex, n*v repeats v):
  //   8b 91 a0 b2 41 29 17 d1 41 e3
endmodule

module mb_dff (
  input  RST,
  input  clk,
  input  D,
  input  WE,
  output Q,
  output out_6
);

  wire and_1_out, and_2_out, and_3_out, G_out, nand_1_out, nand_2_out, nand_3_out, not_1_out, not_2_out,
       or_1_out, or_2_out;

  and and_1 (and_1_out, D, WE);
  not not_1 (not_1_out, WE);
  and and_2 (and_2_out, not_1_out, Q);
  or or_1 (or_1_out, and_1_out, and_2_out);
  nand nand_1 (nand_1_out, nand_3_out, nand_2_out);
  nand nand_2 (nand_2_out, nand_1_out, clk);
  nand G (G_out, nand_2_out, clk, nand_3_out);
  nand nand_3 (nand_3_out, G_out, or_1_out);
  not not_2 (not_2_out, RST);
  or or_2 (or_2_out, RST, nand_2_out);
  and and_3 (and_3_out, not_2_out, G_out);
  nand nand_4 (Q, or_2_out, out_6);
  nand nand_5 (out_6, Q, and_3_out);
endmodule

module PC (
  input  RST,
  input  clk,
  input  WE,
  input  [3:0] D,
  output [3:0] Q
);

  mb_dff mb_dff_1 (.RST(RST), .clk(clk), .D(D[0]), .WE(WE), .Q(Q[0]));  // open: out_6
  mb_dff mb_dff_2 (.RST(RST), .clk(clk), .D(D[1]), .WE(WE), .Q(Q[1]));  // open: out_6
  mb_dff mb_dff_3 (.RST(RST), .clk(clk), .D(D[2]), .WE(WE), .Q(Q[2]));  // open: out_6
  mb_dff mb_dff_4 (.RST(RST), .clk(clk), .D(D[3]), .WE(WE), .Q(Q[3]));  // open: out_6
endmodule

module GPR (
  input  RST,
  input  WE,
  input  clk,
  input  [7:0] D,
  output [7:0] Q
);

  mb_dff mb_dff_1 (.RST(RST), .clk(clk), .D(D[0]), .WE(WE), .Q(Q[0]));  // open: out_6
  mb_dff mb_dff_2 (.RST(RST), .clk(clk), .D(D[1]), .WE(WE), .Q(Q[1]));  // open: out_6
  mb_dff mb_dff_3 (.RST(RST), .clk(clk), .D(D[2]), .WE(WE), .Q(Q[2]));  // open: out_6
  mb_dff mb_dff_4 (.RST(RST), .clk(clk), .D(D[3]), .WE(WE), .Q(Q[3]));  // open: out_6
  mb_dff mb_dff_5 (.RST(RST), .clk(clk), .D(D[4]), .WE(WE), .Q(Q[4]));  // open: out_6
  mb_dff mb_dff_6 (.RST(RST), .clk(clk), .D(D[5]), .WE(WE), .Q(Q[5]));  // open: out_6
  mb_dff mb_dff_7 (.RST(RST), .clk(clk), .D(D[6]), .WE(WE), .Q(Q[6]));  // open: out_6
  mb_dff mb_dff_8 (.RST(RST), .clk(clk), .D(D[7]), .WE(WE), .Q(Q[7]));  // open: out_6
endmodule

module GPRs (
  input  RST,
  input  [7:0] wdata,
  input  clk,
  input  WE,
  input  [1:0] waddr,
  input  [1:0] raddr0,
  input  [1:0] raddr1,
  output [7:0] Q1,
  output [7:0] Q0
);

  wire decoder_1_out0, decoder_1_out1, decoder_1_out2, decoder_1_out3;
  wire [7:0] r0_q, r1_q, r2_q, r3_q;

  Decoder #(.select(2)) decoder_1 (
    .out0(decoder_1_out0), .out1(decoder_1_out1), .out2(decoder_1_out2), .out3(decoder_1_out3), .sel(waddr),
    .en(WE));
  GPR r0 (.RST(RST), .WE(decoder_1_out0), .clk(clk), .D(wdata), .Q(r0_q));
  GPR r1 (.RST(RST), .WE(decoder_1_out1), .clk(clk), .D(wdata), .Q(r1_q));
  GPR r2 (.RST(RST), .WE(decoder_1_out2), .clk(clk), .D(wdata), .Q(r2_q));
  GPR r3 (.RST(RST), .WE(decoder_1_out3), .clk(clk), .D(wdata), .Q(r3_q));
  Multiplexer #(.select(2), .width(8)) multiplexer_1 (
    .in0(r0_q), .in1(r1_q), .in2(r1_q), .in3(r3_q), .out(Q1), .sel(raddr1));
  Multiplexer #(.select(2), .width(8)) multiplexer_2 (
    .in0(r0_q), .in1(r1_q), .in2(r2_q), .in3(r3_q), .out(Q0), .sel(raddr0));
endmodule

module imm (
  input  [3:0] in_1,
  input  in_2,
  input  in_3,
  input  [1:0] in_4,
  output [7:0] out_5,
  output [7:0] Verify
);

  wire clock_1_out;
  wire [3:0] adder_1_out, pc_1_q;

  Clock clock_1 (.out(clock_1_out));
  Adder #(.width(4)) adder_1 (.a(pc_1_q), .b(in_1), .out(adder_1_out));  // open: cin, cout
  PC pc_1 (.RST(in_2), .clk(clock_1_out), .WE(in_3), .D(adder_1_out), .Q(pc_1_q));
  GPRs gprs_1 (
    .RST(in_2), .wdata({4'b0000, out_5[3:0]}), .clk(clock_1_out), .WE(in_3), .waddr(out_5[5:4]),
    .raddr0(in_4), .Q1(Verify));  // open: raddr1, Q0
  ROM #(.addrWidth(4)) rom_1 (.addr(pc_1_q), .data(out_5));

  // Notes on the sheet:
  //   in_1: initial=0x1
  //   contents of rom_1 (hex, n*v repeats v):
  //   8a 90 a0 b1 17 29 d1 df
endmodule

module hex7seg (
  input  D3,
  input  D2,
  input  D1,
  input  D0,
  input  Point,
  input  EN,
  output A,
  output B,
  output C,
  output D,
  output E,
  output F,
  output G,
  output P
);

  wire and_1_out, and_2_out, and_3_out, and_4_out, and_5_out, and_6_out, and_7_out, and_8_out, and_9_out,
       and_10_out, and_11_out, and_12_out, and_13_out, and_14_out, and_15_out, and_16_out, and_17_out,
       and_18_out, and_19_out, and_20_out, nor_1_out, nor_2_out, nor_3_out, nor_4_out, nor_5_out, nor_6_out,
       not_1_out, not_2_out, not_3_out, not_4_out, not_5_out, not_6_out, not_7_out, not_8_out, not_9_out,
       not_10_out, not_11_out, not_12_out, not_13_out, not_14_out, not_15_out, not_16_out, not_17_out,
       not_18_out, not_19_out, not_20_out, not_21_out, not_22_out, not_23_out, not_24_out, not_25_out,
       not_26_out, not_27_out, not_28_out, not_29_out, not_30_out, not_31_out, not_32_out, or_1_out,
       or_2_out, or_3_out, xor_1_out, xor_2_out, xor_3_out, xor_4_out, xor_5_out;

  not not_1 (not_1_out, D3);
  not not_2 (not_2_out, D1);
  not not_3 (not_3_out, D2);
  not not_4 (not_4_out, D0);
  not not_5 (not_5_out, D1);
  not not_6 (not_6_out, D3);
  not not_7 (not_7_out, D3);
  not not_8 (not_8_out, D2);
  not not_9 (not_9_out, D0);
  not not_10 (not_10_out, D0);
  not not_11 (not_11_out, D3);
  not not_12 (not_12_out, D1);
  not not_13 (not_13_out, D1);
  not not_14 (not_14_out, D0);
  not not_15 (not_15_out, D3);
  not not_16 (not_16_out, D2);
  not not_17 (not_17_out, D1);
  not not_18 (not_18_out, D3);
  not not_19 (not_19_out, D2);
  not not_20 (not_20_out, D3);
  not not_21 (not_21_out, D2);
  not not_22 (not_22_out, D1);
  not not_23 (not_23_out, D3);
  not not_24 (not_24_out, D1);
  not not_25 (not_25_out, D3);
  not not_26 (not_26_out, D2);
  not not_27 (not_27_out, D1);
  not not_28 (not_28_out, D3);
  not not_29 (not_29_out, D1);
  not not_30 (not_30_out, D0);
  xor xor_1 (xor_1_out, D2, D0);
  xor xor_2 (xor_2_out, D2, D1);
  xor xor_3 (xor_3_out, D3, D1);
  xor xor_4 (xor_4_out, D2, D0);
  or or_1 (or_1_out, D1, not_10_out);
  xor xor_5 (xor_5_out, D2, D0);
  not not_31 (not_31_out, D2);
  not not_32 (not_32_out, D0);
  and and_1 (and_1_out, D2, not_13_out, not_14_out);
  and and_2 (and_2_out, not_1_out, xor_1_out, not_2_out);
  and and_3 (and_3_out, D3, xor_2_out, D0);
  and and_4 (and_4_out, not_3_out, not_4_out);
  and and_5 (and_5_out, D0, xor_3_out);
  and and_6 (and_6_out, not_5_out, not_6_out, xor_4_out);
  and and_7 (and_7_out, not_7_out, not_8_out, D1, not_9_out);
  and and_8 (and_8_out, D3, D2, or_1_out);
  and and_9 (and_9_out, xor_5_out, not_11_out, not_12_out);
  and and_10 (and_10_out, D2, D1, D0);
  and and_11 (and_11_out, D3, not_31_out, D1, not_32_out);
  or or_2 (or_2_out, and_1_out, D0);
  and and_12 (and_12_out, or_2_out, not_15_out);
  and and_13 (and_13_out, D3, not_16_out, not_17_out, D0);
  and and_14 (and_14_out, not_18_out, not_19_out, D1);
  and and_15 (and_15_out, not_20_out, not_21_out, not_22_out, D0);
  and and_16 (and_16_out, not_23_out, D2, D1, D0);
  and and_17 (and_17_out, D3, D2, not_24_out, D0);
  and and_18 (and_18_out, not_25_out, not_26_out, not_27_out);
  and and_19 (and_19_out, not_28_out, D2, D1, D0);
  and and_20 (and_20_out, D3, D2, not_29_out, not_30_out);
  nor nor_1 (nor_1_out, and_2_out, and_3_out);
  or or_3 (or_3_out, and_4_out, and_5_out, and_6_out);
  nor nor_2 (nor_2_out, and_7_out, and_8_out);
  nor nor_3 (nor_3_out, and_9_out, and_10_out, and_11_out);
  nor nor_4 (nor_4_out, and_12_out, and_13_out);
  nor nor_5 (nor_5_out, and_14_out, and_15_out, and_16_out, and_17_out);
  nor nor_6 (nor_6_out, and_18_out, and_19_out, and_20_out);
  _7_Segment_Display u_7_segment_display_1 (
    .g(nor_6_out), .f(nor_5_out), .a(nor_1_out), .b(or_3_out), .e(nor_4_out), .d(nor_3_out), .c(nor_2_out),
    .dp(Point));
  and and_21 (A, nor_1_out, EN);
  and and_22 (B, or_3_out, EN);
  and and_23 (C, nor_2_out, EN);
  and and_24 (D, nor_3_out, EN);
  and and_25 (E, nor_4_out, EN);
  and and_26 (F, nor_5_out, EN);
  and and_27 (G, nor_6_out, EN);

  assign P = Point;
endmodule
