// Logisim project seq_logic.circ as structural Verilog
module main (
  input  in_1,
  output out_2
);

  wire not_1_out;

  not not_1 (not_1_out, out_2);
  D_Flip_Flop d_flip_flop_1 (.RST(in_1), .D(not_1_out), .Q(out_2));
endmodule

module SR_latch (
  input  R,
  input  S,
  input  in_3,
  input  in_4,
  output Q,
  output Q_overline,
  output out_7,
  output out_8
);

  nor nor_1 (Q, R, Q_overline);
  nor nor_2 (Q_overline, Q, S);
  nand nand_1 (out_7, in_3, out_8);
  nand nand_2 (out_8, out_7, in_4);
endmodule

module D_latch (
  input  RST,
  input  WE,
  input  D,
  output Q,
  output out_5
);

  wire and_1_out, and_2_out, and_3_out, not_1_out, not_2_out, or_1_out;

  not not_1 (not_1_out, D);
  and and_1 (and_1_out, not_1_out, WE);
  and and_2 (and_2_out, WE, D);
  or or_1 (or_1_out, RST, and_1_out);
  not not_2 (not_2_out, RST);
  and and_3 (and_3_out, not_2_out, and_2_out);
  nor nor_1 (Q, or_1_out, out_5);
  nor nor_2 (out_5, Q, and_3_out);
endmodule

module D_Flip_Flop (
  input  RST,
  input  D,
  output Q
);

  wire CLK_out, d_latch_2_q, not_1_out;

  Clock CLK (.out(CLK_out));
  not not_1 (not_1_out, CLK_out);
  D_latch d_latch_1 (.RST(RST), .WE(CLK_out), .D(d_latch_2_q), .Q(Q));  // open: out_5
  D_latch d_latch_2 (.RST(RST), .WE(not_1_out), .D(D), .Q(d_latch_2_q));  // open: out_5
endmodule

module Master_Slave_DFF (
  input  EN,
  input  RST,
  input  clk,
  input  D,
  output Q
);

  wire d_latch_1_q, d_latch_2_q;

  D_latch d_latch_1 (.RST(RST), .WE(clk), .D(d_latch_2_q), .Q(d_latch_1_q));  // open: out_5
  D_latch d_latch_2 (.RST(RST), .WE(clk), .D(D), .Q(d_latch_2_q));  // open: out_5
  and and_1 (Q, EN, d_latch_1_q);
endmodule

module Maintain_Blocking_DFF (
  input  EN,
  input  D,
  output out_3,
  output out_4
);

  wire clk_out, G_out, nand_1_out, nand_2_out, nand_3_out, nand_4_out;

  Clock clk (.out(clk_out));
  nand nand_1 (nand_1_out, nand_3_out, nand_2_out);
  nand nand_2 (nand_2_out, nand_1_out, clk_out);
  nand G (G_out, nand_2_out, clk_out, nand_3_out);
  nand nand_3 (nand_3_out, G_out, D);
  nand nand_4 (nand_4_out, nand_2_out, out_4);
  nand nand_5 (out_4, nand_4_out, G_out);
  and and_1 (out_3, EN, nand_4_out);
endmodule

module register4bit (
  input  EN,
  input  clk,
  input  RST,
  input  [3:0] D,
  output [3:0] out_5
);

  Master_Slave_DFF master_slave_dff_1 (.EN(EN), .RST(RST), .clk(clk), .D(D[0]), .Q(out_5[0]));
  Master_Slave_DFF master_slave_dff_2 (.EN(EN), .RST(RST), .clk(clk), .D(D[1]), .Q(out_5[1]));
  Master_Slave_DFF master_slave_dff_3 (.EN(EN), .RST(RST), .clk(clk), .D(D[2]), .Q(out_5[2]));
  Master_Slave_DFF master_slave_dff_4 (.EN(EN), .RST(RST), .clk(clk), .D(D[3]), .Q(out_5[3]));
endmodule

module adder4bit (
  input  [3:0] A,
  input  [3:0] B,
  input  C,
  output [3:0] out_4
);

  wire fa1bit_1_cout, fa1bit_2_cout, fa1bit_3_cout, fa1bit_4_cout;

  fa1bit fa1bit_1 (.A(A[0]), .B(B[0]), .Cin(C), .S(out_4[0]), .Cout(fa1bit_1_cout));
  fa1bit fa1bit_2 (.A(A[1]), .B(B[1]), .Cin(fa1bit_1_cout), .S(out_4[1]), .Cout(fa1bit_2_cout));
  fa1bit fa1bit_3 (.A(A[2]), .B(B[2]), .Cin(fa1bit_2_cout), .S(out_4[2]), .Cout(fa1bit_3_cout));
  fa1bit fa1bit_4 (.A(A[3]), .B(B[3]), .Cin(fa1bit_3_cout), .S(out_4[3]), .Cout(fa1bit_4_cout));
  LED led_1 (.in(fa1bit_4_cout));
endmodule

module fa1bit (
  input  A,
  input  B,
  input  Cin,
  output S,
  output Cout
);

  wire and_1_out, and_2_out, and_3_out;

  and and_1 (and_1_out, A, B);
  and and_2 (and_2_out, B, Cin);
  and and_3 (and_3_out, A, Cin);
  xor xor_1 (S, A, B, Cin);
  or or_1 (Cout, and_1_out, and_2_out, and_3_out);
endmodule
