// Logisim project xor.circ as structural Verilog: 1 circuit, main circuit main
module main (
  input  in_1,
  input  in_2,
  input  in_3,
  input  in_4,
  output out_5,
  output out_6
);

  wire AND1_out, AND2_out, and_1_out, and_2_out, not_1_out, not_2_out, not_3_out, not_4_out, or_2_out;

  not not_1 (not_1_out, in_2);
  not not_2 (not_2_out, in_1);
  not not_3 (not_3_out, in_4);
  not not_4 (not_4_out, in_3);
  and AND1 (AND1_out, in_1, not_1_out);
  and AND2 (AND2_out, not_2_out, in_2);
  and and_1 (and_1_out, in_3, not_3_out);
  and and_2 (and_2_out, not_4_out, in_4);
  or or_1 (out_5, AND1_out, AND2_out);
  or or_2 (or_2_out, and_1_out, and_2_out);
  not not_5 (out_6, or_2_out);

  // Notes on the sheet:
  //   XOR
  //   NXOR
endmodule
