// Logisim project decoder.circ as structural Verilog: 3 circuits, main circuit main
module main (
  input  A0,
  input  A1,
  input  A3,
  output [7:0] out_4
);

  wire not_1_out;

  not not_1 (not_1_out, A3);
  decoder_24 decoder_24_1 (
    .A0(A0), .A1(A1), .EN(not_1_out), .Y0(out_4[0]), .out_5(out_4[1]), .out_6(out_4[2]), .Y3(out_4[3]));
  decoder_24 decoder_24_2 (.A0(A0), .A1(A1), .EN(A3), .Y0(out_4[4]), .out_5(out_4[5]), .out_6(out_4[6]), .Y3(out_4[7]));
endmodule

module decoder_24 (
  input  A0,
  input  A1,
  input  EN,
  output Y0,
  output out_5,
  output out_6,
  output Y3
);

  wire not_1_out, not_2_out;

  not not_1 (not_1_out, A1);
  not not_2 (not_2_out, A0);
  and and_1 (Y0, not_2_out, EN, not_1_out);
  and and_2 (out_5, A0, EN, not_1_out);
  and and_3 (out_6, not_2_out, EN, A1);
  and and_4 (Y3, A0, EN, A1);
endmodule

module decoder_38 (
  input  A2,
  input  A1,
  input  A0,
  output [7:0] out_4
);

  wire not_1_out, not_2_out, not_3_out;

  not not_1 (not_1_out, A0);
  not not_2 (not_2_out, A1);
  not not_3 (not_3_out, A2);
  and and_1 (out_4[0], not_3_out, not_2_out, not_1_out);
  and and_2 (out_4[1], not_3_out, not_2_out, A0);
  and and_3 (out_4[2], not_3_out, A1, not_1_out);
  and and_4 (out_4[3], not_3_out, A1, A0);
  and and_5 (out_4[4], A2, not_2_out, not_1_out);
  and and_6 (out_4[5], A2, not_2_out, A0);
  and and_7 (out_4[6], A2, A1, not_1_out);
  and and_8 (out_4[7], A2, A1, A0);

  // Notes on the sheet:
  //   Y0
  //   Y7
endmodule
