// Logisim project minirv32.circ as structural Verilog: 8 circuits, main circuit main
module main (
  input  switch,
  input  RST
);

  wire clock_1_out, gpr_interaction_1_gprwe, inst_i_dec_1_gprwe, inst_i_dec_1_ramren, inst_r_dec_1_gprwe,
       inst_s_dec_1_ramwen, inst_u_dec_1_gprwe, or_1_out, rgb_video_1_p3, vgadec_1_ismem;
  wire [3:0] inst_s_dec_1_ramben, rom_1_data_2;
  wire [7:0] inst_s_dec_1_ramwdata, rgb_video_1_p4, rgb_video_1_p5, rom_1_data_3;
  wire [11:0] rom_1_data, rom_1_data_4;
  wire [23:0] rgb_video_1_p6;
  wire [31:0] adder_1_out, gpr_interaction_1_gprwdata, gprs_1_q0, gprs_1_q1, inst_i_dec_1_gprwdata,
       inst_i_dec_1_pcdata, inst_i_dec_1_ramaddr, inst_r_dec_1_gprwdata, inst_s_dec_1_ramaddr,
       inst_u_dec_1_gprwdata, multiplexer_1_out, PC_q, ram_1_dout;

  Clock clock_1 (.out(clock_1_out));
  RAM #(.addrWidth(24), .asyncread("true"), .byteenables("byteEnables"), .dataWidth(32), .\type ("nonvolatile")) ram_1 (
    .addr(multiplexer_1_out[25:2]), .we(vgadec_1_ismem), .oe(inst_i_dec_1_ramren), .clk(clock_1_out),
    .din({inst_s_dec_1_ramwdata, rgb_video_1_p6}), .dout(ram_1_dout), .be3(inst_s_dec_1_ramben[3]),
    .be2(inst_s_dec_1_ramben[2]), .be1(inst_s_dec_1_ramben[1]), .be0(inst_s_dec_1_ramben[0]));
  Register #(.width(32)) PC (.D(inst_i_dec_1_pcdata), .en(switch), .clk(clock_1_out), .Q(PC_q), .clr(RST));
  ROM #(.addrWidth(24), .dataWidth(32)) rom_1 (
    .addr(PC_q[25:2]), .data({rom_1_data_4, rom_1_data_3, rom_1_data[11], rom_1_data_2, rom_1_data[6:0]}));
  Adder #(.width(32)) adder_1 (.a(32'h4), .b(PC_q), .out(adder_1_out));  // open: cin, cout
  // RGB_Video #(.cursor("No Cursor"), .height(256), .width(256)) rgb_video_1: pin names not known; wires that end beside it: RST, clock_1_out, rgb_video_1_p3, rgb_video_1_p4, rgb_video_1_p5, rgb_video_1_p6
  Inst_I_dec inst_i_dec_1 (
    .opc(rom_1_data[6:0]), .funct3(rom_1_data_3[2:0]), .imm(rom_1_data_4), .rs1data(gprs_1_q0),
    .PCplus4(adder_1_out), .RAMdata(ram_1_dout), .GPRwe(inst_i_dec_1_gprwe), .RAMaddr(inst_i_dec_1_ramaddr),
    .RAMren(inst_i_dec_1_ramren), .GPRwdata(inst_i_dec_1_gprwdata), .PCdata(inst_i_dec_1_pcdata));
  Inst_R_dec inst_r_dec_1 (
    .opc(rom_1_data[6:0]), .funct3(rom_1_data_3[2:0]), .funct7(rom_1_data_4[11:5]), .rs1data(gprs_1_q0),
    .rs2data(gprs_1_q1), .GPRwe(inst_r_dec_1_gprwe), .GPRwdata(inst_r_dec_1_gprwdata));
  Inst_U_dec inst_u_dec_1 (
    .opc(rom_1_data[6:0]), .imm({rom_1_data_4, rom_1_data_3}), .GPRwe(inst_u_dec_1_gprwe),
    .GPRwdata(inst_u_dec_1_gprwdata));
  Inst_S_dec inst_s_dec_1 (
    .opc(rom_1_data[6:0]), .imm0to4({rom_1_data[11], rom_1_data_2}), .funct3(rom_1_data_3[2:0]),
    .imm5to11(rom_1_data_4[11:5]), .rs1data(gprs_1_q0), .rs2data(gprs_1_q1), .RAMwen(inst_s_dec_1_ramwen),
    .RAMben(inst_s_dec_1_ramben), .RAMaddr(inst_s_dec_1_ramaddr),
    .RAMwdata({inst_s_dec_1_ramwdata, rgb_video_1_p6}));
  Multiplexer #(.disabled("Z"), .enable("true"), .width(32)) multiplexer_1 (
    .in0(inst_s_dec_1_ramaddr), .in1(inst_i_dec_1_ramaddr), .out(multiplexer_1_out),
    .sel(inst_i_dec_1_ramren), .en(or_1_out));
  or or_1 (or_1_out, inst_i_dec_1_ramren, vgadec_1_ismem);
  GPRs gprs_1 (
    .clk(clock_1_out), .wdata(gpr_interaction_1_gprwdata), .waddr(rom_1_data_2),
    .WE(gpr_interaction_1_gprwe), .raddr0(rom_1_data_3[6:3]), .raddr1(rom_1_data_4[3:0]), .RST(RST),
    .Q0(gprs_1_q0), .Q1(gprs_1_q1));
  GPR_Interaction gpr_interaction_1 (
    .Iwe(inst_i_dec_1_gprwe), .Rwe(inst_r_dec_1_gprwe), .Uwe(inst_u_dec_1_gprwe),
    .Iwdata(inst_i_dec_1_gprwdata), .Rwdata(inst_r_dec_1_gprwdata), .Uwdata(inst_u_dec_1_gprwdata),
    .GPRwdata(gpr_interaction_1_gprwdata), .GPRwe(gpr_interaction_1_gprwe));
  VGAdec vgadec_1 (
    .RAMwen(inst_s_dec_1_ramwen), .RAMwaddr(inst_s_dec_1_ramaddr), .isMem(vgadec_1_ismem),
    .isVGA(rgb_video_1_p3), .X(rgb_video_1_p4), .Y(rgb_video_1_p5));

  // Notes on the sheet:
  //   contents of rom_1 (hex, n*v repeats v):
  //   413 93137 10113 10b7 dbc08093 80e7 fe012823 fea10923 fea12423 fe914203 fe4109a3 ff012783 f787b3
  //   f787b3 4b6b7 f0068693 fdc10113 d787b3 10000713 f12423 10593 100793 b00513 2112023 12023 12223 e12623
  //   e12823 f10a23 10b7 a8408093 80e7 2012083 2410113 8067 ff410113 112423 10b7 a7c08093 80e7 513 1800093
  //   80e7 812083 513 c10113 8067 852583 feb12823 fe812e23 3437 a0840413 ff014183 3401b3 1c183 ff114203
  //   440233 24203 4181b3 ff214203 440233 24203 4181b3 ff314203 440233 24203 4181b3 3237 a0020213 320233
  //   24203 ffc12403 420233 420233 410233 11b7 85c18193 fe312823 14800193 fe312623 fec22203 20067 1052703
  //   52683 452783 fe810113 e12423 112a23 fed12823 fef12623 13737 c0070713 fe012223 ff314203 fe4102a3
  //   fef14203 fe410223 fe412203 470233 24203 fe4105a3 ff214203 fe4102a3 fee14203 fe410223 fe412203 470233
  //   24203 fe410523 ff114203 fe4102a3 fed14203 fe410223 fe412203 470233 24203 fe4104a3 ff014203 fe4102a3
  //   fec14203 fe410223 fe412203 470233 24203 fe410423 fe812703 c52603 fee12823 fe812e23 3437 a0840413
  //   ff014183 3401b3 1c183 ff114203 440233 24203 4181b3 ff214203 440233 24203 4181b3 ff314203 440233
  //   24203 4181b3 3237 a0020213 320233 24203 ffc12403 420233 420233 410233 66800193 fe312823 28000193
  //   fe312623 fec22203 20067 c68733 10000513 fe812e23 fe912c23 fee12823 50413 ff012483 fe812423 feb14183
  //   3181b3 fe312423 fe914183 3181b3 fe912423 feb14203 420233 fe412423 fe914203 4181b3 3181b3 fe312a23
  //   fe912423 33237 b0020213 feb14183 4181b3 1c183 fe3103a3 fea14183 4181b3 1c183 fe310323 fe914183
  //   4181b3 1c183 fe3102a3 fe814183 4181b3 1c183 fe310223 ff412183 fe412203 440233 120213 fe412423
  //   feb14203 420233 fe412423 fe914203 4181b3 3237 b0820213 320233 ff812483 ffc12403 24203 420233 420233
  //   410233 11b7 86018193 fe312823 38800193 fe312623 fec22203 20067 812703 10000513 812823 e78733
  //   fe812e23 fe912c23 fee12823 50413 ff012483 fe812423 feb14183 3181b3 fe312423 fe914183 3181b3 fe912423
  //   feb14203 420233 fe412423 fe914203 4181b3 3181b3 fe312a23 fe912423 33237 b0020213 feb14183 4181b3
  //   1c183 fe3103a3 fea14183 4181b3 1c183 fe310323 fe914183 4181b3 1c183 fe3102a3 fe814183 4181b3 1c183
  //   fe310223 ff412183 fe412203 440233 120213 fe412423 feb14203 420233 fe412423 fe914203 4181b3 3237
  //   b0820213 320233 ff812483 ffc12403 24203 420233 420233 410233 11b7 86418193 fe312823 49800193
  //   fe312623 fec22203 20067 8*f787b3 d787b3 f787b3 f787b3 20000437 f40433 812783 c60633 c60633 fef12423
  //   feb14183 3181b3 fe312423 fe914183 fff78213 fe412423 feb14203 420233 fe412423 fe914203 4181b3 3237
  //   b1820213 418233 24203 420233 420233 410233 65800193 fe312823 53c00193 fe312623 fec22203 20067 912623
  //   493 40513 c12223 b12023 10b7 de008093 80e7 12583 412603 812783 148493 40040413 c585b3 fef12823
  //   fe912623 fe812e23 fe912c23 4b437 d0040413 ff014183 340233 100193 320023 fec14183 3401b3 18023 24183
  //   ff114483 940233 100493 920023 fed14483 9404b3 48023 24483 9181b3 ff214483 940233 100493 920023
  //   fee14483 9404b3 48023 24483 9181b3 ff314483 940233 100493 920023 fef14483 9404b3 48023 24483 9181b3
  //   3237 a0020213 320233 24203 ff812483 ffc12403 420233 420233 410233 65400193 fe312823 54400193
  //   fe312623 fec22203 20067 c12483 1012403 1412083 1810113 8067 10000713 fec12823 fee12623 fe812e23
  //   fe912c23 4b437 d0040413 ff014183 340233 100193 320023 fec14183 3401b3 18023 24183 ff114483 940233
  //   100493 920023 fed14483 9404b3 48023 24483 9181b3 ff214483 940233 100493 920023 fee14483 9404b3 48023
  //   24483 9181b3 ff314483 940233 100493 920023 fef14483 9404b3 48023 24483 9181b3 3237 a0020213 320233
  //   24203 ff812483 ffc12403 420233 420233 410233 74c00193 fe312823 28000193 fe312623 fec22203 20067
  //   812703 fee12823 fec12623 fe812e23 fe912c23 4b437 d0040413 ff014183 340233 100193 320023 fec14183
  //   3401b3 18023 24183 ff114483 940233 100493 920023 fed14483 9404b3 48023 24483 9181b3 ff214483 940233
  //   100493 920023 fee14483 9404b3 48023 24483 9181b3 ff314483 940233 100493 920023 fef14483 9404b3 48023
  //   24483 9181b3 3237 a0020213 320233 24203 ff812483 ffc12403 420233 420233 410233 11b7 83418193
  //   fe312823 38800193 fe312623 fec22203 20067 1412083 40637 20000537 1810113 1237 de020213 20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
endmodule

module GPRs (
  input  clk,
  input  [31:0] wdata,
  input  [3:0] waddr,
  input  WE,
  input  [3:0] raddr0,
  input  [3:0] raddr1,
  input  RST,
  output [31:0] Q0,
  output [31:0] Q1
);

  wire decoder_1_out1, decoder_1_out2, decoder_1_out3, decoder_1_out4, decoder_1_out5, decoder_1_out6,
       decoder_1_out7, decoder_1_out8, decoder_1_out9, decoder_1_out10, decoder_1_out11, decoder_1_out12,
       decoder_1_out13, decoder_1_out14, decoder_1_out15;
  wire [31:0] register_1_q, register_2_q, register_3_q, register_4_q, register_5_q, register_6_q,
       register_7_q, register_8_q, register_9_q, register_10_q, register_11_q, register_12_q, register_13_q,
       register_14_q, register_15_q;

  Decoder #(.select(4)) decoder_1 (
    .out1(decoder_1_out1), .out2(decoder_1_out2), .out3(decoder_1_out3), .out4(decoder_1_out4),
    .out5(decoder_1_out5), .out6(decoder_1_out6), .out7(decoder_1_out7), .out8(decoder_1_out8),
    .out9(decoder_1_out9), .out10(decoder_1_out10), .out11(decoder_1_out11), .out12(decoder_1_out12),
    .out13(decoder_1_out13), .out14(decoder_1_out14), .out15(decoder_1_out15), .sel(waddr), .en(WE));  // open: out0
  Register #(.width(32)) register_1 (.D(wdata), .en(decoder_1_out8), .clk(clk), .Q(register_1_q), .clr(RST));
  Register #(.width(32)) register_2 (.D(wdata), .en(decoder_1_out1), .clk(clk), .Q(register_2_q), .clr(RST));
  Register #(.width(32)) register_3 (.D(wdata), .en(decoder_1_out9), .clk(clk), .Q(register_3_q), .clr(RST));
  Register #(.width(32)) register_4 (.D(wdata), .en(decoder_1_out2), .clk(clk), .Q(register_4_q), .clr(RST));
  Register #(.width(32)) register_5 (.D(wdata), .en(decoder_1_out10), .clk(clk), .Q(register_5_q), .clr(RST));
  Register #(.width(32)) register_6 (.D(wdata), .en(decoder_1_out3), .clk(clk), .Q(register_6_q), .clr(RST));
  Register #(.width(32)) register_7 (.D(wdata), .en(decoder_1_out11), .clk(clk), .Q(register_7_q), .clr(RST));
  Register #(.width(32)) register_8 (.D(wdata), .en(decoder_1_out4), .clk(clk), .Q(register_8_q), .clr(RST));
  Register #(.width(32)) register_9 (.D(wdata), .en(decoder_1_out12), .clk(clk), .Q(register_9_q), .clr(RST));
  Register #(.width(32)) register_10 (.D(wdata), .en(decoder_1_out5), .clk(clk), .Q(register_10_q), .clr(RST));
  Register #(.width(32)) register_11 (.D(wdata), .en(decoder_1_out13), .clk(clk), .Q(register_11_q), .clr(RST));
  Register #(.width(32)) register_12 (.D(wdata), .en(decoder_1_out6), .clk(clk), .Q(register_12_q), .clr(RST));
  Register #(.width(32)) register_13 (.D(wdata), .en(decoder_1_out14), .clk(clk), .Q(register_13_q), .clr(RST));
  Register #(.width(32)) register_14 (.D(wdata), .en(decoder_1_out7), .clk(clk), .Q(register_14_q), .clr(RST));
  Register #(.width(32)) register_15 (.D(wdata), .en(decoder_1_out15), .clk(clk), .Q(register_15_q), .clr(RST));
  Multiplexer #(.select(4), .width(32)) multiplexer_1 (
    .in0({32{1'b0}}), .in1(register_2_q), .in2(register_4_q), .in3(register_6_q), .in4(register_8_q),
    .in5(register_10_q), .in6(register_12_q), .in7(register_14_q), .in8(register_1_q), .in9(register_3_q),
    .in10(register_5_q), .in11(register_7_q), .in12(register_9_q), .in13(register_11_q),
    .in14(register_13_q), .in15(register_15_q), .out(Q0), .sel(raddr0));
  Multiplexer #(.select(4), .width(32)) multiplexer_2 (
    .in0({32{1'b0}}), .in1(register_2_q), .in2(register_4_q), .in3(register_6_q), .in4(register_8_q),
    .in5(register_10_q), .in6(register_12_q), .in7(register_14_q), .in8(register_1_q), .in9(register_3_q),
    .in10(register_5_q), .in11(register_7_q), .in12(register_9_q), .in13(register_11_q),
    .in14(register_13_q), .in15(register_15_q), .out(Q1), .sel(raddr1));
endmodule

module Inst_I_dec (
  input  [6:0] opc,
  input  [2:0] funct3,
  input  [11:0] imm,
  input  [31:0] rs1data,
  input  [31:0] PCplus4,
  input  [31:0] RAMdata,
  output GPRwe,
  output [31:0] RAMaddr,
  output RAMren,
  output [31:0] GPRwdata,
  output [31:0] PCdata
);

  wire addi_out, comparator_1_eq, comparator_2_eq, comparator_3_eq, comparator_4_eq, comparator_5_eq,
       comparator_6_eq, jalr_out, lbu_out, lw_out;
  wire [7:0] multiplexer_1_out;
  wire [31:0] adder_1_out, and_1_out, bit_extender_1_out, bit_extender_2_out, multiplexer_4_out;

  Multiplexer #(.select(2), .width(8)) multiplexer_1 (
    .in0(RAMdata[7:0]), .in1(RAMdata[15:8]), .in2(RAMdata[23:16]), .in3(RAMdata[31:24]),
    .out(multiplexer_1_out), .sel(RAMaddr[1:0]));
  Comparator #(.width(7)) comparator_1 (.a(opc), .b(7'b0010011), .eq(comparator_1_eq));  // open: gt, lt
  Comparator #(.width(7)) comparator_2 (.a(opc), .b(7'b1100111), .eq(comparator_2_eq));  // open: gt, lt
  Comparator #(.width(7)) comparator_3 (.a(opc), .b(7'b0000011), .eq(comparator_3_eq));  // open: gt, lt
  Comparator #(.width(3)) comparator_4 (.a(funct3), .b(3'b000), .eq(comparator_4_eq));  // open: gt, lt
  Comparator #(.width(3)) comparator_5 (.a(funct3), .b(3'b100), .eq(comparator_5_eq));  // open: gt, lt
  Comparator #(.width(3)) comparator_6 (.a(funct3), .b(3'b010), .eq(comparator_6_eq));  // open: gt, lt
  assign bit_extender_1_out = {{20{imm[11]}}, imm};  // Bit_Extender bit_extender_1
  assign bit_extender_2_out = {{24{1'b0}}, multiplexer_1_out};  // Bit_Extender bit_extender_2
  Adder #(.width(32)) adder_1 (.a(bit_extender_1_out), .b(rs1data), .out(adder_1_out));  // open: cin, cout
  and addi (addi_out, comparator_1_eq, comparator_4_eq);
  and jalr (jalr_out, comparator_2_eq, comparator_4_eq);
  and lbu (lbu_out, comparator_5_eq, comparator_3_eq);
  and lw (lw_out, comparator_3_eq, comparator_6_eq);
  assign and_1_out = adder_1_out & 32'hfffffffe;  // AND_Gate and_1, 32 bits wide
  Multiplexer #(.width(32)) multiplexer_2 (.in0(adder_1_out), .in1(PCplus4), .out(RAMaddr), .sel(jalr_out));
  Multiplexer #(.width(32)) multiplexer_3 (.in0(PCplus4), .in1(and_1_out), .out(PCdata), .sel(jalr_out));
  Multiplexer #(.width(32)) multiplexer_4 (
    .in0(bit_extender_2_out), .in1(RAMdata), .out(multiplexer_4_out), .sel(lw_out));
  or or_1 (GPRwe, addi_out, jalr_out, lbu_out, lw_out);
  or Load (RAMren, lw_out, lbu_out);
  Multiplexer #(.width(32)) multiplexer_5 (.in0(RAMaddr), .in1(multiplexer_4_out), .out(GPRwdata), .sel(RAMren));
endmodule

module Inst_R_dec (
  input  [6:0] opc,
  input  [2:0] funct3,
  input  [6:0] funct7,
  input  [31:0] rs1data,
  input  [31:0] rs2data,
  output GPRwe,
  output [31:0] GPRwdata
);

  wire comparator_1_eq, comparator_2_eq, comparator_3_eq;

  Comparator #(.width(7)) comparator_1 (.a(opc), .b(7'b0110011), .eq(comparator_1_eq));  // open: gt, lt
  Comparator #(.width(3)) comparator_2 (.a(funct3), .b(3'b000), .eq(comparator_2_eq));  // open: gt, lt
  Comparator #(.width(7)) comparator_3 (.a(funct7), .b({7{1'b0}}), .eq(comparator_3_eq));  // open: gt, lt
  Adder #(.width(32)) adder_1 (.a(rs1data), .b(rs2data), .out(GPRwdata));  // open: cin, cout
  and add (GPRwe, comparator_1_eq, comparator_2_eq, comparator_3_eq);
endmodule

module Inst_U_dec (
  input  [6:0] opc,
  input  [19:0] imm,
  output GPRwe,
  output [31:0] GPRwdata
);

  Comparator #(.width(7)) comparator_1 (.a(opc), .b(7'b0110111), .eq(GPRwe));  // open: gt, lt

  assign GPRwdata = {imm, {12{1'b0}}};
endmodule

module Inst_S_dec (
  input  [6:0] opc,
  input  [4:0] imm0to4,
  input  [2:0] funct3,
  input  [6:0] imm5to11,
  input  [31:0] rs1data,
  input  [31:0] rs2data,
  output RAMwen,
  output [3:0] RAMben,
  output [31:0] RAMaddr,
  output [31:0] RAMwdata
);

  wire comparator_1_eq, comparator_2_eq, comparator_3_eq, sb_out, sw_out;
  wire [3:0] decoder_1_out0;
  wire [31:0] bit_extender_1_out;

  Comparator #(.width(7)) comparator_1 (.a(opc), .b(7'b0100011), .eq(comparator_1_eq));  // open: gt, lt
  Comparator #(.width(3)) comparator_2 (.a(funct3), .b(3'b000), .eq(comparator_2_eq));  // open: gt, lt
  Comparator #(.width(3)) comparator_3 (.a(3'b010), .b(funct3), .eq(comparator_3_eq));  // open: gt, lt
  assign bit_extender_1_out = {{20{imm5to11[6]}}, {imm5to11, imm0to4}};  // Bit_Extender bit_extender_1
  and sb (sb_out, comparator_1_eq, comparator_2_eq);
  and sw (sw_out, comparator_1_eq, comparator_3_eq);
  Adder #(.width(32)) adder_1 (.a(bit_extender_1_out), .b(rs1data), .out(RAMaddr));  // open: cin, cout
  Multiplexer #(.width(32)) multiplexer_1 (
    .in0({rs2data[7:0], rs2data[7:0], rs2data[7:0], rs2data[7:0]}), .in1(rs2data), .out(RAMwdata),
    .sel(comparator_3_eq));
  Decoder #(.enable("false"), .select(2)) decoder_1 (
    .out0(decoder_1_out0[0]), .out1(decoder_1_out0[1]), .out2(decoder_1_out0[2]), .out3(decoder_1_out0[3]),
    .sel(RAMaddr[1:0]));
  Multiplexer #(.width(4)) multiplexer_2 (.in0(decoder_1_out0), .in1(4'b1111), .out(RAMben), .sel(sw_out));
  or S (RAMwen, sb_out, sw_out);
endmodule

module GPR_Interaction (
  input  Iwe,
  input  Rwe,
  input  Uwe,
  input  [31:0] Iwdata,
  input  [31:0] Rwdata,
  input  [31:0] Uwdata,
  output [31:0] GPRwdata,
  output GPRwe
);

  wire [31:0] and_1_out, and_2_out, and_3_out, bit_extender_1_out, bit_extender_2_out, bit_extender_3_out;

  or or_1 (GPRwe, Iwe, Rwe, Uwe);
  assign bit_extender_1_out = {{31{Iwe}}, Iwe};  // Bit_Extender bit_extender_1
  assign and_1_out = bit_extender_1_out & Iwdata;  // AND_Gate and_1, 32 bits wide
  assign bit_extender_2_out = {{31{Rwe}}, Rwe};  // Bit_Extender bit_extender_2
  assign and_2_out = bit_extender_2_out & Rwdata;  // AND_Gate and_2, 32 bits wide
  assign bit_extender_3_out = {{31{Uwe}}, Uwe};  // Bit_Extender bit_extender_3
  assign and_3_out = bit_extender_3_out & Uwdata;  // AND_Gate and_3, 32 bits wide
  assign GPRwdata = and_1_out | and_2_out | and_3_out;  // OR_Gate or_2, 32 bits wide
endmodule

module VGAdec (
  input  RAMwen,
  input  [31:0] RAMwaddr,
  output isMem,
  output isVGA,
  output [7:0] X,
  output [7:0] Y
);

  wire and_1_out, comparator_1_gt, comparator_2_eq, comparator_2_gt, not_1_out, or_1_out;

  Comparator #(.width(32)) comparator_1 (.a(32'h20040000), .b(RAMwaddr), .gt(comparator_1_gt));  // open: eq, lt
  Comparator #(.width(32)) comparator_2 (
    .a(RAMwaddr), .b(32'h20000000), .gt(comparator_2_gt), .eq(comparator_2_eq));  // open: lt
  or or_1 (or_1_out, comparator_2_gt, comparator_2_eq);
  and and_1 (and_1_out, comparator_1_gt, or_1_out);
  not not_1 (not_1_out, and_1_out);
  and and_2 (isMem, not_1_out, RAMwen);
  and and_3 (isVGA, RAMwen, and_1_out);

  assign X = RAMwaddr[9:2];
  assign Y = RAMwaddr[17:10];
endmodule
