// Logisim project xor.circ as structural Verilog: 1 circuit, main circuit main
module main (
  input  in_1,
  input  in_2,
  output out_3
);

  wire AND1_out, AND2_out, not_1_out, not_2_out;

  not not_1 (not_1_out, in_2);
  not not_2 (not_2_out, in_1);
  and AND1 (AND1_out, in_1, not_1_out);
  and AND2 (AND2_out, not_2_out, in_2);
  or or_1 (out_3, AND1_out, AND2_out);

  // Notes on the sheet:
  //   XOR
endmodule
