// Logisim project add.circ as structural Verilog: 7 circuits, main circuit main
module main (
  input  [4:0] A,
  input  [4:0] B,
  input  C,
  output [4:0] out_4
);

  wire fa1bit_1_cout, fa1bit_2_cout, fa1bit_3_cout, fa1bit_4_cout, fa1bit_5_cout;
  wire [3:0] fa4bit_1_p1;

  // fa4bit fa4bit_1: pin names not known; wires that end beside it: fa4bit_1_p1
  fa1bit fa1bit_1 (.A(A[0]), .B(B[0]), .Cin(C), .S(out_4[0]), .Cout(fa1bit_1_cout));
  fa1bit fa1bit_2 (.A(A[1]), .B(B[1]), .Cin(fa1bit_1_cout), .S(out_4[1]), .Cout(fa1bit_2_cout));
  fa1bit fa1bit_3 (.A(A[2]), .B(B[2]), .Cin(fa1bit_2_cout), .S(out_4[2]), .Cout(fa1bit_3_cout));
  fa1bit fa1bit_4 (.A(A[3]), .B(B[3]), .Cin(fa1bit_3_cout), .S(out_4[3]), .Cout(fa1bit_4_cout));
  fa1bit fa1bit_5 (.A(A[4]), .B(B[4]), .Cin(fa1bit_4_cout), .S(out_4[4]), .Cout(fa1bit_5_cout));
  LED led_1 (.in(fa1bit_5_cout));
  bcd7seg bcd7seg_1 (
    .D3(fa4bit_1_p1[3]), .D2(fa4bit_1_p1[2]), .D1(fa4bit_1_p1[1]), .D0(fa4bit_1_p1[0]));  // open: EN, Point, A, B, C, D, E, F, G, P
endmodule

module fa1bit (
  input  A,
  input  B,
  input  Cin,
  output S,
  output Cout
);

  wire and_1_out, and_2_out, and_3_out;

  and and_1 (and_1_out, A, B);
  and and_2 (and_2_out, B, Cin);
  and and_3 (and_3_out, A, Cin);
  xor xor_1 (S, A, B, Cin);
  or or_1 (Cout, and_1_out, and_2_out, and_3_out);
endmodule

module ha1bit (
  input  A,
  input  B,
  output S,
  output Cout
);

  xor xor_1 (S, A, B);
  and and_1 (Cout, A, B);
endmodule

module fa1bit_based_ha (
  input  A,
  input  B,
  input  Cin,
  output C1,
  output S
);

  wire H0_cout, H0_s, H1_cout;

  ha1bit H0 (.A(A), .B(B), .S(H0_s), .Cout(H0_cout));
  ha1bit H1 (.A(H0_s), .B(Cin), .S(S), .Cout(H1_cout));
  or or_1 (C1, H0_cout, H1_cout);
endmodule

module hex7seg (
  input  D3,
  input  D2,
  input  D1,
  input  D0,
  input  Point,
  input  EN,
  output A,
  output B,
  output C,
  output D,
  output E,
  output F,
  output G,
  output P
);

  wire and_1_out, and_2_out, and_3_out, and_4_out, and_5_out, and_6_out, and_7_out, and_8_out, and_9_out,
       and_10_out, and_11_out, and_12_out, and_13_out, and_14_out, and_15_out, and_16_out, and_17_out,
       and_18_out, and_19_out, and_20_out, nor_1_out, nor_2_out, nor_3_out, nor_4_out, nor_5_out, nor_6_out,
       not_1_out, not_2_out, not_3_out, not_4_out, not_5_out, not_6_out, not_7_out, not_8_out, not_9_out,
       not_10_out, not_11_out, not_12_out, not_13_out, not_14_out, not_15_out, not_16_out, not_17_out,
       not_18_out, not_19_out, not_20_out, not_21_out, not_22_out, not_23_out, not_24_out, not_25_out,
       not_26_out, not_27_out, not_28_out, not_29_out, not_30_out, not_31_out, not_32_out, or_1_out,
       or_2_out, or_3_out, xor_1_out, xor_2_out, xor_3_out, xor_4_out, xor_5_out;

  not not_1 (not_1_out, D3);
  not not_2 (not_2_out, D1);
  not not_3 (not_3_out, D2);
  not not_4 (not_4_out, D0);
  not not_5 (not_5_out, D1);
  not not_6 (not_6_out, D3);
  not not_7 (not_7_out, D3);
  not not_8 (not_8_out, D2);
  not not_9 (not_9_out, D0);
  not not_10 (not_10_out, D0);
  not not_11 (not_11_out, D3);
  not not_12 (not_12_out, D1);
  not not_13 (not_13_out, D1);
  not not_14 (not_14_out, D0);
  not not_15 (not_15_out, D3);
  not not_16 (not_16_out, D2);
  not not_17 (not_17_out, D1);
  not not_18 (not_18_out, D3);
  not not_19 (not_19_out, D2);
  not not_20 (not_20_out, D3);
  not not_21 (not_21_out, D2);
  not not_22 (not_22_out, D1);
  not not_23 (not_23_out, D3);
  not not_24 (not_24_out, D1);
  not not_25 (not_25_out, D3);
  not not_26 (not_26_out, D2);
  not not_27 (not_27_out, D1);
  not not_28 (not_28_out, D3);
  not not_29 (not_29_out, D1);
  not not_30 (not_30_out, D0);
  xor xor_1 (xor_1_out, D2, D0);
  xor xor_2 (xor_2_out, D2, D1);
  xor xor_3 (xor_3_out, D3, D1);
  xor xor_4 (xor_4_out, D2, D0);
  or or_1 (or_1_out, D1, not_10_out);
  xor xor_5 (xor_5_out, D2, D0);
  not not_31 (not_31_out, D2);
  not not_32 (not_32_out, D0);
  and and_1 (and_1_out, D2, not_13_out, not_14_out);
  and and_2 (and_2_out, not_1_out, xor_1_out, not_2_out);
  and and_3 (and_3_out, D3, xor_2_out, D0);
  and and_4 (and_4_out, not_3_out, not_4_out);
  and and_5 (and_5_out, D0, xor_3_out);
  and and_6 (and_6_out, not_5_out, not_6_out, xor_4_out);
  and and_7 (and_7_out, not_7_out, not_8_out, D1, not_9_out);
  and and_8 (and_8_out, D3, D2, or_1_out);
  and and_9 (and_9_out, xor_5_out, not_11_out, not_12_out);
  and and_10 (and_10_out, D2, D1, D0);
  and and_11 (and_11_out, D3, not_31_out, D1, not_32_out);
  or or_2 (or_2_out, and_1_out, D0);
  and and_12 (and_12_out, or_2_out, not_15_out);
  and and_13 (and_13_out, D3, not_16_out, not_17_out, D0);
  and and_14 (and_14_out, not_18_out, not_19_out, D1);
  and and_15 (and_15_out, not_20_out, not_21_out, not_22_out, D0);
  and and_16 (and_16_out, not_23_out, D2, D1, D0);
  and and_17 (and_17_out, D3, D2, not_24_out, D0);
  and and_18 (and_18_out, not_25_out, not_26_out, not_27_out);
  and and_19 (and_19_out, not_28_out, D2, D1, D0);
  and and_20 (and_20_out, D3, D2, not_29_out, not_30_out);
  nor nor_1 (nor_1_out, and_2_out, and_3_out);
  or or_3 (or_3_out, and_4_out, and_5_out, and_6_out);
  nor nor_2 (nor_2_out, and_7_out, and_8_out);
  nor nor_3 (nor_3_out, and_9_out, and_10_out, and_11_out);
  nor nor_4 (nor_4_out, and_12_out, and_13_out);
  nor nor_5 (nor_5_out, and_14_out, and_15_out, and_16_out, and_17_out);
  nor nor_6 (nor_6_out, and_18_out, and_19_out, and_20_out);
  _7_Segment_Display u_7_segment_display_1 (
    .g(nor_6_out), .f(nor_5_out), .a(nor_1_out), .b(or_3_out), .e(nor_4_out), .d(nor_3_out), .c(nor_2_out),
    .dp(Point));
  and and_21 (A, nor_1_out, EN);
  and and_22 (B, or_3_out, EN);
  and and_23 (C, nor_2_out, EN);
  and and_24 (D, nor_3_out, EN);
  and and_25 (E, nor_4_out, EN);
  and and_26 (F, nor_5_out, EN);
  and and_27 (G, nor_6_out, EN);

  assign P = Point;
endmodule

module fa4bit (
  input  [3:0] A,
  input  [3:0] B,
  input  C,
  output [3:0] out_4
);

  wire fa1bit_1_cout, fa1bit_2_cout, fa1bit_3_cout, fa1bit_4_cout;

  fa1bit fa1bit_1 (.A(A[0]), .B(B[0]), .Cin(C), .S(out_4[0]), .Cout(fa1bit_1_cout));
  fa1bit fa1bit_2 (.A(A[1]), .B(B[1]), .Cin(fa1bit_1_cout), .S(out_4[1]), .Cout(fa1bit_2_cout));
  fa1bit fa1bit_3 (.A(A[2]), .B(B[2]), .Cin(fa1bit_2_cout), .S(out_4[2]), .Cout(fa1bit_3_cout));
  fa1bit fa1bit_4 (.A(A[3]), .B(B[3]), .Cin(fa1bit_3_cout), .S(out_4[3]), .Cout(fa1bit_4_cout));
  LED led_1 (.in(fa1bit_4_cout));
endmodule

module bcd7seg (
  input  D3,
  input  D2,
  input  D1,
  input  D0,
  input  EN,
  input  Point,
  output A,
  output B,
  output C,
  output D,
  output E,
  output F,
  output G,
  output P
);

  wire and_1_out, and_2_out, and_3_out, and_4_out, and_5_out, and_6_out, and_7_out, and_8_out, and_9_out,
       and_10_out, and_11_out, and_12_out, and_13_out, and_14_out, and_15_out, and_16_out, not_1_out,
       not_2_out, not_3_out, or_1_out, or_2_out, or_3_out, or_4_out, or_5_out, or_6_out, or_7_out;

  not not_1 (not_1_out, D2);
  not not_2 (not_2_out, D1);
  not not_3 (not_3_out, D0);
  and and_1 (and_1_out, D2, D0);
  and and_2 (and_2_out, not_1_out, not_3_out);
  and and_3 (and_3_out, D1, D0);
  and and_4 (and_4_out, not_2_out, not_3_out);
  and and_5 (and_5_out, D1, not_3_out);
  and and_6 (and_6_out, D1, not_1_out);
  and and_7 (and_7_out, not_1_out, not_3_out);
  and and_8 (and_8_out, D2, not_2_out, D0);
  and and_9 (and_9_out, D1, not_3_out);
  and and_10 (and_10_out, not_1_out, not_3_out);
  and and_11 (and_11_out, D2, not_3_out);
  and and_12 (and_12_out, D2, not_2_out);
  and and_13 (and_13_out, not_2_out, not_3_out);
  and and_14 (and_14_out, D1, not_3_out);
  and and_15 (and_15_out, D1, not_1_out);
  and and_16 (and_16_out, D2, not_2_out);
  or or_1 (or_1_out, and_1_out, D3, D1, and_2_out);
  or or_2 (or_2_out, and_3_out, not_1_out, and_4_out);
  or or_3 (or_3_out, D2, not_2_out, D0);
  or or_4 (or_4_out, and_5_out, and_6_out, D3, and_7_out, and_8_out);
  or or_5 (or_5_out, and_9_out, and_10_out);
  or or_6 (or_6_out, D3, and_11_out, and_12_out, and_13_out);
  or or_7 (or_7_out, D3, and_14_out, and_15_out, and_16_out);
  _7_Segment_Display u_7_segment_display_1 (
    .g(or_7_out), .f(or_6_out), .a(or_1_out), .b(or_2_out), .e(or_5_out), .d(or_4_out), .c(or_3_out),
    .dp(Point));
  and and_17 (A, or_1_out, EN);
  and and_18 (B, or_2_out, EN);
  and and_19 (C, or_3_out, EN);
  and and_20 (D, or_4_out, EN);
  and and_21 (E, or_5_out, EN);
  and and_22 (F, or_6_out, EN);
  and and_23 (G, or_7_out, EN);

  assign P = Point;
endmodule
