// Logisim project elec_clock.circ as structural Verilog: 12 circuits, main circuit main
module main (
  input  [3:0] step,
  input  start,
  input  [3:0] reset,
  input  RST,
  input  [3:0] in_5,
  input  display,
  input  [3:0] in_7,
  input  [3:0] in_8,
  input  [3:0] in_9
);

  wire and_1_out, and_2_out, and_3_out, and_4_out, and_5_out, bcd7seg_1_a, bcd7seg_1_b, bcd7seg_1_c,
       bcd7seg_1_d, bcd7seg_1_e, bcd7seg_1_f, bcd7seg_1_g, bcd7seg_1_p, bcd7seg_2_a, bcd7seg_2_b,
       bcd7seg_2_c, bcd7seg_2_d, bcd7seg_2_e, bcd7seg_2_f, bcd7seg_2_g, bcd7seg_2_p, bcd7seg_3_a,
       bcd7seg_3_b, bcd7seg_3_c, bcd7seg_3_d, bcd7seg_3_e, bcd7seg_3_f, bcd7seg_3_g, bcd7seg_3_p,
       bcd7seg_4_a, bcd7seg_4_b, bcd7seg_4_c, bcd7seg_4_d, bcd7seg_4_e, bcd7seg_4_f, bcd7seg_4_g,
       bcd7seg_4_p, bcd7seg_5_a, bcd7seg_5_b, bcd7seg_5_c, bcd7seg_5_d, bcd7seg_5_e, bcd7seg_5_f,
       bcd7seg_5_g, bcd7seg_5_p, bcd7seg_6_a, bcd7seg_6_b, bcd7seg_6_c, bcd7seg_6_d, bcd7seg_6_e,
       bcd7seg_6_f, bcd7seg_6_g, bcd7seg_6_p, clk_out, comparator4bit_1_same, comparator4bit_2_same,
       comparator4bit_3_same, comparator4bit_4_same, comparator4bit_5_same, comparator4bit_6_same;
  wire [3:0] adder4bit_1_s, adder4bit_2_s, adder4bit_3_s, adder4bit_4_s, adder4bit_5_s, adder4bit_6_s,
       mux4bit2sel1_1_d, mux4bit2sel1_2_d, mux4bit2sel1_3_d, mux4bit2sel1_4_d, mux4bit2sel1_5_d,
       mux4bit2sel1_6_d, mux4bit2sel1_7_d, register_1_q, register_2_q, register_3_q, register_4_q,
       register_5_q, register_6_q;

  Clock clk (.out(clk_out));
  adder4bit adder4bit_1 (.A(register_1_q), .B(step), .S(adder4bit_1_s));  // open: C
  adder4bit adder4bit_2 (.A(register_2_q), .B(step), .S(adder4bit_2_s));  // open: C
  adder4bit adder4bit_3 (.A(register_3_q), .B(step), .S(adder4bit_3_s));  // open: C
  adder4bit adder4bit_4 (.A(register_4_q), .B(step), .S(adder4bit_4_s));  // open: C
  adder4bit adder4bit_5 (.A(register_5_q), .B(step), .S(adder4bit_5_s));  // open: C
  adder4bit adder4bit_6 (.A(register_6_q), .B(step), .S(adder4bit_6_s));  // open: C
  mux4bit2sel1 mux4bit2sel1_1 (.S0(comparator4bit_1_same), .D0(adder4bit_1_s), .D1(reset), .D(mux4bit2sel1_1_d));
  mux4bit2sel1 mux4bit2sel1_2 (.S0(comparator4bit_2_same), .D0(adder4bit_2_s), .D1(reset), .D(mux4bit2sel1_2_d));
  mux4bit2sel1 mux4bit2sel1_3 (.S0(comparator4bit_3_same), .D0(adder4bit_3_s), .D1(reset), .D(mux4bit2sel1_3_d));
  mux4bit2sel1 mux4bit2sel1_4 (.S0(comparator4bit_4_same), .D0(adder4bit_4_s), .D1(reset), .D(mux4bit2sel1_4_d));
  mux4bit2sel1 mux4bit2sel1_5 (.S0(comparator4bit_5_same), .D0(adder4bit_5_s), .D1(reset), .D(mux4bit2sel1_5_d));
  mux4bit2sel1 mux4bit2sel1_6 (.S0(comparator4bit_6_same), .D0(adder4bit_6_s), .D1(reset), .D(mux4bit2sel1_6_d));
  Register #(.width(4)) register_1 (.D(mux4bit2sel1_1_d), .en(start), .clk(clk_out), .Q(register_1_q), .clr(RST));
  Register #(.width(4)) register_2 (
    .D(mux4bit2sel1_2_d), .en(comparator4bit_1_same), .clk(clk_out), .Q(register_2_q), .clr(RST));
  and and_1 (and_1_out, comparator4bit_2_same, comparator4bit_1_same);
  Register #(.width(4)) register_3 (.D(mux4bit2sel1_3_d), .en(and_1_out), .clk(clk_out), .Q(register_3_q), .clr(RST));
  and and_2 (and_2_out, and_1_out, comparator4bit_3_same);
  Register #(.width(4)) register_4 (.D(mux4bit2sel1_4_d), .en(and_2_out), .clk(clk_out), .Q(register_4_q), .clr(RST));
  and and_3 (and_3_out, and_2_out, comparator4bit_4_same);
  Register #(.width(4)) register_5 (.D(mux4bit2sel1_5_d), .en(and_3_out), .clk(clk_out), .Q(register_5_q), .clr(RST));
  and and_4 (and_4_out, comparator4bit_5_same, and_3_out);
  Register #(.width(4)) register_6 (.D(mux4bit2sel1_6_d), .en(and_4_out), .clk(clk_out), .Q(register_6_q), .clr(RST));
  and and_5 (and_5_out, and_3_out, comparator4bit_6_same);
  mux4bit2sel1 mux4bit2sel1_7 (.S0(and_5_out), .D0(in_5), .D1(in_8), .D(mux4bit2sel1_7_d));
  bcd7seg bcd7seg_1 (
    .D0(register_1_q[0]), .D1(register_1_q[1]), .D2(register_1_q[2]), .D3(register_1_q[3]), .EN(display),
    .A(bcd7seg_1_a), .B(bcd7seg_1_b), .C(bcd7seg_1_c), .D(bcd7seg_1_d), .E(bcd7seg_1_e), .F(bcd7seg_1_f),
    .G(bcd7seg_1_g), .P(bcd7seg_1_p));  // open: Point
  comparator4bit comparator4bit_1 (.A(register_1_q), .B(in_5), .Same(comparator4bit_1_same));
  bcd7seg bcd7seg_2 (
    .D0(register_2_q[0]), .D1(register_2_q[1]), .D2(register_2_q[2]), .D3(register_2_q[3]), .EN(display),
    .A(bcd7seg_2_a), .B(bcd7seg_2_b), .C(bcd7seg_2_c), .D(bcd7seg_2_d), .E(bcd7seg_2_e), .F(bcd7seg_2_f),
    .G(bcd7seg_2_g), .P(bcd7seg_2_p));  // open: Point
  comparator4bit comparator4bit_2 (.A(register_2_q), .B(in_7), .Same(comparator4bit_2_same));
  bcd7seg bcd7seg_3 (
    .D0(register_3_q[0]), .D1(register_3_q[1]), .D2(register_3_q[2]), .D3(register_3_q[3]), .EN(display),
    .A(bcd7seg_3_a), .B(bcd7seg_3_b), .C(bcd7seg_3_c), .D(bcd7seg_3_d), .E(bcd7seg_3_e), .F(bcd7seg_3_f),
    .G(bcd7seg_3_g), .P(bcd7seg_3_p));  // open: Point
  comparator4bit comparator4bit_3 (.A(register_3_q), .B(in_5), .Same(comparator4bit_3_same));
  bcd7seg bcd7seg_4 (
    .D0(register_4_q[0]), .D1(register_4_q[1]), .D2(register_4_q[2]), .D3(register_4_q[3]), .EN(display),
    .A(bcd7seg_4_a), .B(bcd7seg_4_b), .C(bcd7seg_4_c), .D(bcd7seg_4_d), .E(bcd7seg_4_e), .F(bcd7seg_4_f),
    .G(bcd7seg_4_g), .P(bcd7seg_4_p));  // open: Point
  comparator4bit comparator4bit_4 (.A(register_4_q), .B(in_7), .Same(comparator4bit_4_same));
  bcd7seg bcd7seg_5 (
    .D0(register_5_q[0]), .D1(register_5_q[1]), .D2(register_5_q[2]), .D3(register_5_q[3]), .EN(display),
    .A(bcd7seg_5_a), .B(bcd7seg_5_b), .C(bcd7seg_5_c), .D(bcd7seg_5_d), .E(bcd7seg_5_e), .F(bcd7seg_5_f),
    .G(bcd7seg_5_g), .P(bcd7seg_5_p));  // open: Point
  comparator4bit comparator4bit_5 (.A(register_5_q), .B(mux4bit2sel1_7_d), .Same(comparator4bit_5_same));
  bcd7seg bcd7seg_6 (
    .D0(register_6_q[0]), .D1(register_6_q[1]), .D2(register_6_q[2]), .D3(register_6_q[3]), .EN(display),
    .A(bcd7seg_6_a), .B(bcd7seg_6_b), .C(bcd7seg_6_c), .D(bcd7seg_6_d), .E(bcd7seg_6_e), .F(bcd7seg_6_f),
    .G(bcd7seg_6_g), .P(bcd7seg_6_p));  // open: Point
  comparator4bit comparator4bit_6 (.A(register_6_q), .B(in_9), .Same(comparator4bit_6_same));
  _7_Segment_Display u_7_segment_display_1 (
    .g(bcd7seg_6_g), .f(bcd7seg_6_f), .a(bcd7seg_6_a), .b(bcd7seg_6_b), .e(bcd7seg_6_e), .d(bcd7seg_6_d),
    .c(bcd7seg_6_c), .dp(bcd7seg_6_p));
  _7_Segment_Display u_7_segment_display_2 (
    .g(bcd7seg_5_g), .f(bcd7seg_5_f), .a(bcd7seg_5_a), .b(bcd7seg_5_b), .e(bcd7seg_5_e), .d(bcd7seg_5_d),
    .c(bcd7seg_5_c), .dp(bcd7seg_5_p));
  _7_Segment_Display u_7_segment_display_3 (
    .g(bcd7seg_4_g), .f(bcd7seg_4_f), .a(bcd7seg_4_a), .b(bcd7seg_4_b), .e(bcd7seg_4_e), .d(bcd7seg_4_d),
    .c(bcd7seg_4_c), .dp(bcd7seg_4_p));
  _7_Segment_Display u_7_segment_display_4 (
    .g(bcd7seg_3_g), .f(bcd7seg_3_f), .a(bcd7seg_3_a), .b(bcd7seg_3_b), .e(bcd7seg_3_e), .d(bcd7seg_3_d),
    .c(bcd7seg_3_c), .dp(bcd7seg_3_p));
  _7_Segment_Display u_7_segment_display_5 (
    .g(bcd7seg_2_g), .f(bcd7seg_2_f), .a(bcd7seg_2_a), .b(bcd7seg_2_b), .e(bcd7seg_2_e), .d(bcd7seg_2_d),
    .c(bcd7seg_2_c), .dp(bcd7seg_2_p));
  _7_Segment_Display u_7_segment_display_6 (
    .g(bcd7seg_1_g), .f(bcd7seg_1_f), .a(bcd7seg_1_a), .b(bcd7seg_1_b), .e(bcd7seg_1_e), .d(bcd7seg_1_d),
    .c(bcd7seg_1_c), .dp(bcd7seg_1_p));

  // Notes on the sheet:
  //   step: initial=0x1
  //   start: initial=0x1
  //   in_8: initial=0x3
  //   in_5: initial=0x9
  //   in_7: initial=0x5
  //   in_9: initial=0x2
endmodule

module bcd7seg (
  input  D0,
  input  D1,
  input  D2,
  input  D3,
  input  EN,
  input  Point,
  output A,
  output B,
  output C,
  output D,
  output E,
  output F,
  output G,
  output P
);

  wire and_1_out, and_2_out, and_3_out, and_4_out, and_5_out, and_6_out, and_7_out, and_8_out, and_9_out,
       and_10_out, and_11_out, and_12_out, and_13_out, and_14_out, and_15_out, and_16_out, not_1_out,
       not_2_out, not_3_out, or_1_out, or_2_out, or_3_out, or_4_out, or_5_out, or_6_out, or_7_out;

  not not_1 (not_1_out, D0);
  not not_2 (not_2_out, D1);
  not not_3 (not_3_out, D2);
  and and_1 (and_1_out, D2, D0);
  and and_2 (and_2_out, not_3_out, not_1_out);
  and and_3 (and_3_out, D1, D0);
  and and_4 (and_4_out, not_2_out, not_1_out);
  and and_5 (and_5_out, D1, not_1_out);
  and and_6 (and_6_out, D1, not_3_out);
  and and_7 (and_7_out, not_3_out, not_1_out);
  and and_8 (and_8_out, D2, not_2_out, D0);
  and and_9 (and_9_out, D1, not_1_out);
  and and_10 (and_10_out, not_3_out, not_1_out);
  and and_11 (and_11_out, D2, not_1_out);
  and and_12 (and_12_out, D2, not_2_out);
  and and_13 (and_13_out, not_2_out, not_1_out);
  and and_14 (and_14_out, D1, not_1_out);
  and and_15 (and_15_out, D1, not_3_out);
  and and_16 (and_16_out, D2, not_2_out);
  or or_1 (or_1_out, and_1_out, D3, D1, and_2_out);
  or or_2 (or_2_out, and_3_out, not_3_out, and_4_out);
  or or_3 (or_3_out, D2, not_2_out, D0);
  or or_4 (or_4_out, and_5_out, and_6_out, D3, and_7_out, and_8_out);
  or or_5 (or_5_out, and_9_out, and_10_out);
  or or_6 (or_6_out, D3, and_11_out, and_12_out, and_13_out);
  or or_7 (or_7_out, D3, and_14_out, and_15_out, and_16_out);
  _7_Segment_Display u_7_segment_display_1 (
    .g(or_7_out), .f(or_6_out), .a(or_1_out), .b(or_2_out), .e(or_5_out), .d(or_4_out), .c(or_3_out),
    .dp(Point));
  and and_17 (A, or_1_out, EN);
  and and_18 (B, or_2_out, EN);
  and and_19 (C, or_3_out, EN);
  and and_20 (D, or_4_out, EN);
  and and_21 (E, or_5_out, EN);
  and and_22 (F, or_6_out, EN);
  and and_23 (G, or_7_out, EN);

  assign P = Point;
endmodule

module d_latch (
  input  RST,
  input  WE,
  input  D,
  output Q,
  output out_5
);

  wire and_1_out, and_2_out, and_3_out, not_1_out, not_2_out, or_1_out;

  not not_1 (not_1_out, D);
  and and_1 (and_1_out, not_1_out, WE);
  and and_2 (and_2_out, WE, D);
  or or_1 (or_1_out, RST, and_1_out);
  not not_2 (not_2_out, RST);
  and and_3 (and_3_out, not_2_out, and_2_out);
  nor nor_1 (Q, or_1_out, out_5);
  nor nor_2 (out_5, Q, and_3_out);
endmodule

module ms_dff (
  input  RST,
  input  clk,
  input  D,
  input  WE,
  output Q
);

  wire and_1_out, and_2_out, d_latch_2_q, not_1_out, or_1_out;

  not not_1 (not_1_out, WE);
  and and_1 (and_1_out, D, WE);
  or or_1 (or_1_out, and_1_out, and_2_out);
  and and_2 (and_2_out, not_1_out, Q);
  d_latch d_latch_1 (.RST(RST), .WE(clk), .D(d_latch_2_q), .Q(Q));  // open: out_5
  d_latch d_latch_2 (.RST(RST), .WE(clk), .D(or_1_out), .Q(d_latch_2_q));  // open: out_5
endmodule

module mb_dff (
  input  RST,
  input  clk,
  input  D,
  input  WE,
  output Q,
  output out_6
);

  wire and_1_out, and_2_out, and_3_out, G_out, nand_1_out, nand_2_out, nand_3_out, not_1_out, not_2_out,
       or_1_out, or_2_out;

  and and_1 (and_1_out, D, WE);
  not not_1 (not_1_out, WE);
  and and_2 (and_2_out, not_1_out, Q);
  or or_1 (or_1_out, and_1_out, and_2_out);
  nand nand_1 (nand_1_out, nand_3_out, nand_2_out);
  nand nand_2 (nand_2_out, nand_1_out, clk);
  nand G (G_out, nand_2_out, clk, nand_3_out);
  nand nand_3 (nand_3_out, G_out, or_1_out);
  not not_2 (not_2_out, RST);
  or or_2 (or_2_out, RST, nand_2_out);
  and and_3 (and_3_out, not_2_out, G_out);
  nand nand_4 (Q, or_2_out, out_6);
  nand nand_5 (out_6, Q, and_3_out);
endmodule

module register4bit (
  input  RST,
  input  clk,
  input  WE,
  input  [3:0] D,
  output [3:0] Q
);

  mb_dff mb_dff_1 (.RST(RST), .clk(clk), .D(D[0]), .WE(WE), .Q(Q[0]));  // open: out_6
  mb_dff mb_dff_2 (.RST(RST), .clk(clk), .D(D[1]), .WE(WE), .Q(Q[1]));  // open: out_6
  mb_dff mb_dff_3 (.RST(RST), .clk(clk), .D(D[2]), .WE(WE), .Q(Q[2]));  // open: out_6
  mb_dff mb_dff_4 (.RST(RST), .clk(clk), .D(D[3]), .WE(WE), .Q(Q[3]));  // open: out_6
endmodule

module full_adder (
  input  A,
  input  B,
  input  Cin,
  output S,
  output Cout
);

  wire and_1_out, and_2_out, and_3_out;

  and and_1 (and_1_out, A, B);
  and and_2 (and_2_out, B, Cin);
  and and_3 (and_3_out, A, Cin);
  xor xor_1 (S, A, B, Cin);
  or or_1 (Cout, and_1_out, and_2_out, and_3_out);
endmodule

module adder4bit (
  input  [3:0] A,
  input  [3:0] B,
  input  C,
  output [3:0] S
);

  wire full_adder_1_cout, full_adder_2_cout, full_adder_3_cout, full_adder_4_cout;

  full_adder full_adder_1 (.A(A[0]), .B(B[0]), .Cin(C), .S(S[0]), .Cout(full_adder_1_cout));
  full_adder full_adder_2 (.A(A[1]), .B(B[1]), .Cin(full_adder_1_cout), .S(S[1]), .Cout(full_adder_2_cout));
  full_adder full_adder_3 (.A(A[2]), .B(B[2]), .Cin(full_adder_2_cout), .S(S[2]), .Cout(full_adder_3_cout));
  full_adder full_adder_4 (.A(A[3]), .B(B[3]), .Cin(full_adder_3_cout), .S(S[3]), .Cout(full_adder_4_cout));
  LED led_1 (.in(full_adder_4_cout));
endmodule

module comparator4bit (
  input  [3:0] A,
  input  [3:0] B,
  output Same
);

  wire xnor_1_out, xnor_2_out, xnor_3_out, xnor_4_out;

  xnor xnor_1 (xnor_1_out, A[0], B[0]);
  xnor xnor_2 (xnor_2_out, A[1], B[1]);
  xnor xnor_3 (xnor_3_out, A[2], B[2]);
  xnor xnor_4 (xnor_4_out, A[3], B[3]);
  and and_1 (Same, xnor_1_out, xnor_2_out, xnor_3_out, xnor_4_out);
endmodule

module mux4bit2sel1 (
  input  S0,
  input  [3:0] D0,
  input  [3:0] D1,
  output [3:0] D
);

  wire and_1_out, and_2_out, and_3_out, and_4_out, and_5_out, and_6_out, and_7_out, and_8_out, dec1to2_1_y0,
       dec1to2_1_y1;

  dec1to2 dec1to2_1 (.A0(S0), .Y0(dec1to2_1_y0), .Y1(dec1to2_1_y1));
  and and_1 (and_1_out, D0[0], dec1to2_1_y0);
  and and_2 (and_2_out, D1[0], dec1to2_1_y1);
  and and_3 (and_3_out, D0[1], dec1to2_1_y0);
  and and_4 (and_4_out, D1[1], dec1to2_1_y1);
  and and_5 (and_5_out, D0[2], dec1to2_1_y0);
  and and_6 (and_6_out, D1[2], dec1to2_1_y1);
  and and_7 (and_7_out, D0[3], dec1to2_1_y0);
  and and_8 (and_8_out, D1[3], dec1to2_1_y1);
  or or_1 (D[0], and_1_out, and_2_out);
  or or_2 (D[1], and_3_out, and_4_out);
  or or_3 (D[2], and_5_out, and_6_out);
  or or_4 (D[3], and_7_out, and_8_out);
endmodule

module dec1to2 (
  input  A0,
  output Y0,
  output Y1
);

  not not_1 (Y0, A0);

  assign Y1 = A0;
endmodule

module original_build (
  input  [3:0] step,
  input  [3:0] reset,
  input  start,
  input  RST,
  input  [3:0] in_5,
  input  display,
  input  [3:0] in_7,
  input  [3:0] in_8,
  input  [3:0] in_9
);

  wire and_1_out, and_2_out, and_3_out, and_4_out, and_5_out, bcd7seg_1_a, bcd7seg_1_b, bcd7seg_1_c,
       bcd7seg_1_d, bcd7seg_1_e, bcd7seg_1_f, bcd7seg_1_g, bcd7seg_1_p, bcd7seg_2_a, bcd7seg_2_b,
       bcd7seg_2_c, bcd7seg_2_d, bcd7seg_2_e, bcd7seg_2_f, bcd7seg_2_g, bcd7seg_2_p, bcd7seg_3_a,
       bcd7seg_3_b, bcd7seg_3_c, bcd7seg_3_d, bcd7seg_3_e, bcd7seg_3_f, bcd7seg_3_g, bcd7seg_3_p,
       bcd7seg_4_a, bcd7seg_4_b, bcd7seg_4_c, bcd7seg_4_d, bcd7seg_4_e, bcd7seg_4_f, bcd7seg_4_g,
       bcd7seg_4_p, bcd7seg_5_a, bcd7seg_5_b, bcd7seg_5_c, bcd7seg_5_d, bcd7seg_5_e, bcd7seg_5_f,
       bcd7seg_5_g, bcd7seg_5_p, bcd7seg_6_a, bcd7seg_6_b, bcd7seg_6_c, bcd7seg_6_d, bcd7seg_6_e,
       bcd7seg_6_f, bcd7seg_6_g, bcd7seg_6_p, clk_out, comparator4bit_1_same, comparator4bit_2_same,
       comparator4bit_3_same, comparator4bit_4_same, comparator4bit_5_same, comparator4bit_6_same;
  wire [3:0] adder4bit_1_s, adder4bit_2_s, adder4bit_3_s, adder4bit_4_s, adder4bit_5_s, adder4bit_6_s,
       mux4bit2sel1_1_d, mux4bit2sel1_2_d, mux4bit2sel1_3_d, mux4bit2sel1_4_d, mux4bit2sel1_5_d,
       mux4bit2sel1_6_d, mux4bit2sel1_7_d, register4bit_1_q, register4bit_2_q, register4bit_3_q,
       register4bit_4_q, register4bit_5_q, register4bit_6_q;

  Clock clk (.out(clk_out));
  adder4bit adder4bit_1 (.A(register4bit_1_q), .B(step), .S(adder4bit_1_s));  // open: C
  adder4bit adder4bit_2 (.A(register4bit_2_q), .B(step), .S(adder4bit_2_s));  // open: C
  adder4bit adder4bit_3 (.A(register4bit_3_q), .B(step), .S(adder4bit_3_s));  // open: C
  adder4bit adder4bit_4 (.A(register4bit_4_q), .B(step), .S(adder4bit_4_s));  // open: C
  adder4bit adder4bit_5 (.A(register4bit_5_q), .B(step), .S(adder4bit_5_s));  // open: C
  adder4bit adder4bit_6 (.A(register4bit_6_q), .B(step), .S(adder4bit_6_s));  // open: C
  mux4bit2sel1 mux4bit2sel1_1 (.S0(comparator4bit_1_same), .D0(adder4bit_1_s), .D1(reset), .D(mux4bit2sel1_1_d));
  mux4bit2sel1 mux4bit2sel1_2 (.S0(comparator4bit_2_same), .D0(adder4bit_2_s), .D1(reset), .D(mux4bit2sel1_2_d));
  mux4bit2sel1 mux4bit2sel1_3 (.S0(comparator4bit_3_same), .D0(adder4bit_3_s), .D1(reset), .D(mux4bit2sel1_3_d));
  mux4bit2sel1 mux4bit2sel1_4 (.S0(comparator4bit_4_same), .D0(adder4bit_4_s), .D1(reset), .D(mux4bit2sel1_4_d));
  mux4bit2sel1 mux4bit2sel1_5 (.S0(comparator4bit_5_same), .D0(adder4bit_5_s), .D1(reset), .D(mux4bit2sel1_5_d));
  mux4bit2sel1 mux4bit2sel1_6 (.S0(comparator4bit_6_same), .D0(adder4bit_6_s), .D1(reset), .D(mux4bit2sel1_6_d));
  and and_1 (and_1_out, comparator4bit_1_same, comparator4bit_2_same);
  and and_2 (and_2_out, and_1_out, comparator4bit_3_same);
  and and_3 (and_3_out, and_2_out, comparator4bit_4_same);
  and and_4 (and_4_out, comparator4bit_5_same, and_3_out);
  and and_5 (and_5_out, and_3_out, comparator4bit_6_same);
  register4bit register4bit_1 (.RST(RST), .clk(clk_out), .WE(start), .D(mux4bit2sel1_1_d), .Q(register4bit_1_q));
  register4bit register4bit_2 (
    .RST(RST), .clk(clk_out), .WE(comparator4bit_1_same), .D(mux4bit2sel1_2_d), .Q(register4bit_2_q));
  register4bit register4bit_3 (.RST(RST), .clk(clk_out), .WE(and_1_out), .D(mux4bit2sel1_3_d), .Q(register4bit_3_q));
  register4bit register4bit_4 (.RST(RST), .clk(clk_out), .WE(and_2_out), .D(mux4bit2sel1_4_d), .Q(register4bit_4_q));
  register4bit register4bit_5 (.RST(RST), .clk(clk_out), .WE(and_3_out), .D(mux4bit2sel1_5_d), .Q(register4bit_5_q));
  register4bit register4bit_6 (.RST(RST), .clk(clk_out), .WE(and_4_out), .D(mux4bit2sel1_6_d), .Q(register4bit_6_q));
  mux4bit2sel1 mux4bit2sel1_7 (.S0(and_5_out), .D0(in_5), .D1(in_8), .D(mux4bit2sel1_7_d));
  bcd7seg bcd7seg_1 (
    .D0(register4bit_1_q[0]), .D1(register4bit_1_q[1]), .D2(register4bit_1_q[2]), .D3(register4bit_1_q[3]),
    .EN(display), .A(bcd7seg_1_a), .B(bcd7seg_1_b), .C(bcd7seg_1_c), .D(bcd7seg_1_d), .E(bcd7seg_1_e),
    .F(bcd7seg_1_f), .G(bcd7seg_1_g), .P(bcd7seg_1_p));  // open: Point
  comparator4bit comparator4bit_1 (.A(register4bit_1_q), .B(in_5), .Same(comparator4bit_1_same));
  bcd7seg bcd7seg_2 (
    .D0(register4bit_2_q[0]), .D1(register4bit_2_q[1]), .D2(register4bit_2_q[2]), .D3(register4bit_2_q[3]),
    .EN(display), .A(bcd7seg_2_a), .B(bcd7seg_2_b), .C(bcd7seg_2_c), .D(bcd7seg_2_d), .E(bcd7seg_2_e),
    .F(bcd7seg_2_f), .G(bcd7seg_2_g), .P(bcd7seg_2_p));  // open: Point
  comparator4bit comparator4bit_2 (.A(register4bit_2_q), .B(in_7), .Same(comparator4bit_2_same));
  bcd7seg bcd7seg_3 (
    .D0(register4bit_3_q[0]), .D1(register4bit_3_q[1]), .D2(register4bit_3_q[2]), .D3(register4bit_3_q[3]),
    .EN(display), .A(bcd7seg_3_a), .B(bcd7seg_3_b), .C(bcd7seg_3_c), .D(bcd7seg_3_d), .E(bcd7seg_3_e),
    .F(bcd7seg_3_f), .G(bcd7seg_3_g), .P(bcd7seg_3_p));  // open: Point
  comparator4bit comparator4bit_3 (.A(register4bit_3_q), .B(in_5), .Same(comparator4bit_3_same));
  bcd7seg bcd7seg_4 (
    .D0(register4bit_4_q[0]), .D1(register4bit_4_q[1]), .D2(register4bit_4_q[2]), .D3(register4bit_4_q[3]),
    .EN(display), .A(bcd7seg_4_a), .B(bcd7seg_4_b), .C(bcd7seg_4_c), .D(bcd7seg_4_d), .E(bcd7seg_4_e),
    .F(bcd7seg_4_f), .G(bcd7seg_4_g), .P(bcd7seg_4_p));  // open: Point
  comparator4bit comparator4bit_4 (.A(register4bit_4_q), .B(in_7), .Same(comparator4bit_4_same));
  bcd7seg bcd7seg_5 (
    .D0(register4bit_5_q[0]), .D1(register4bit_5_q[1]), .D2(register4bit_5_q[2]), .D3(register4bit_5_q[3]),
    .EN(display), .A(bcd7seg_5_a), .B(bcd7seg_5_b), .C(bcd7seg_5_c), .D(bcd7seg_5_d), .E(bcd7seg_5_e),
    .F(bcd7seg_5_f), .G(bcd7seg_5_g), .P(bcd7seg_5_p));  // open: Point
  comparator4bit comparator4bit_5 (.A(register4bit_5_q), .B(mux4bit2sel1_7_d), .Same(comparator4bit_5_same));
  bcd7seg bcd7seg_6 (
    .D0(register4bit_6_q[0]), .D1(register4bit_6_q[1]), .D2(register4bit_6_q[2]), .D3(register4bit_6_q[3]),
    .EN(display), .A(bcd7seg_6_a), .B(bcd7seg_6_b), .C(bcd7seg_6_c), .D(bcd7seg_6_d), .E(bcd7seg_6_e),
    .F(bcd7seg_6_f), .G(bcd7seg_6_g), .P(bcd7seg_6_p));  // open: Point
  comparator4bit comparator4bit_6 (.A(register4bit_6_q), .B(in_9), .Same(comparator4bit_6_same));
  _7_Segment_Display u_7_segment_display_1 (
    .g(bcd7seg_6_g), .f(bcd7seg_6_f), .a(bcd7seg_6_a), .b(bcd7seg_6_b), .e(bcd7seg_6_e), .d(bcd7seg_6_d),
    .c(bcd7seg_6_c), .dp(bcd7seg_6_p));
  _7_Segment_Display u_7_segment_display_2 (
    .g(bcd7seg_5_g), .f(bcd7seg_5_f), .a(bcd7seg_5_a), .b(bcd7seg_5_b), .e(bcd7seg_5_e), .d(bcd7seg_5_d),
    .c(bcd7seg_5_c), .dp(bcd7seg_5_p));
  _7_Segment_Display u_7_segment_display_3 (
    .g(bcd7seg_4_g), .f(bcd7seg_4_f), .a(bcd7seg_4_a), .b(bcd7seg_4_b), .e(bcd7seg_4_e), .d(bcd7seg_4_d),
    .c(bcd7seg_4_c), .dp(bcd7seg_4_p));
  _7_Segment_Display u_7_segment_display_4 (
    .g(bcd7seg_3_g), .f(bcd7seg_3_f), .a(bcd7seg_3_a), .b(bcd7seg_3_b), .e(bcd7seg_3_e), .d(bcd7seg_3_d),
    .c(bcd7seg_3_c), .dp(bcd7seg_3_p));
  _7_Segment_Display u_7_segment_display_5 (
    .g(bcd7seg_2_g), .f(bcd7seg_2_f), .a(bcd7seg_2_a), .b(bcd7seg_2_b), .e(bcd7seg_2_e), .d(bcd7seg_2_d),
    .c(bcd7seg_2_c), .dp(bcd7seg_2_p));
  _7_Segment_Display u_7_segment_display_6 (
    .g(bcd7seg_1_g), .f(bcd7seg_1_f), .a(bcd7seg_1_a), .b(bcd7seg_1_b), .e(bcd7seg_1_e), .d(bcd7seg_1_d),
    .c(bcd7seg_1_c), .dp(bcd7seg_1_p));

  // Notes on the sheet:
  //   step: initial=0x1
  //   start: initial=0x1
  //   in_8: initial=0x3
  //   in_5: initial=0x9
  //   in_7: initial=0x5
  //   in_9: initial=0x2
endmodule
