// Logisim project encoder.circ as structural Verilog: 6 circuits, main circuit main
module main (
  input  A15,
  input  A14,
  input  A13,
  input  A12,
  input  A11,
  input  A10,
  input  A9,
  input  A8,
  input  in_9,
  input  A7,
  input  A6,
  input  A5,
  input  A4,
  input  in_14,
  input  A3,
  input  A2,
  input  A1,
  input  A0
);

  wire hex7seg_1_a, hex7seg_1_b, hex7seg_1_c, hex7seg_1_d, hex7seg_1_e, hex7seg_1_f, hex7seg_1_g,
       hex7seg_1_p, priority_encoder_16_4_1_y0, priority_encoder_16_4_1_y1, priority_encoder_16_4_1_y2,
       priority_encoder_16_4_1_y3;

  priority_encoder_16_4 priority_encoder_16_4_1 (
    .A15(A15), .A14(A14), .A13(A13), .A12(A12), .A11(A11), .A10(A10), .A9(A9), .A8(A8), .A7(A7), .A6(A6),
    .A5(A5), .A4(A4), .A3(A3), .A2(A2), .A1(A1), .A0(A0), .EN(in_14), .Y3(priority_encoder_16_4_1_y3),
    .Y2(priority_encoder_16_4_1_y2), .Y1(priority_encoder_16_4_1_y1), .Y0(priority_encoder_16_4_1_y0));
  _7_Segment_Display u_7_segment_display_1 (
    .g(hex7seg_1_g), .f(hex7seg_1_f), .a(hex7seg_1_a), .b(hex7seg_1_b), .e(hex7seg_1_e), .d(hex7seg_1_d),
    .c(hex7seg_1_c), .dp(hex7seg_1_p));
  hex7seg hex7seg_1 (
    .D3(priority_encoder_16_4_1_y3), .D2(priority_encoder_16_4_1_y2), .D1(priority_encoder_16_4_1_y1),
    .D0(priority_encoder_16_4_1_y0), .EN(in_9), .A(hex7seg_1_a), .B(hex7seg_1_b), .C(hex7seg_1_c),
    .D(hex7seg_1_d), .E(hex7seg_1_e), .F(hex7seg_1_f), .G(hex7seg_1_g), .P(hex7seg_1_p));  // open: Point
endmodule

module hex7seg (
  input  D3,
  input  D2,
  input  D1,
  input  D0,
  input  Point,
  input  EN,
  output A,
  output B,
  output C,
  output D,
  output E,
  output F,
  output G,
  output P
);

  wire and_1_out, and_2_out, and_3_out, and_4_out, and_5_out, and_6_out, and_7_out, and_8_out, and_9_out,
       and_10_out, and_11_out, and_12_out, and_13_out, and_14_out, and_15_out, and_16_out, and_17_out,
       and_18_out, and_19_out, and_20_out, nor_1_out, nor_2_out, nor_3_out, nor_4_out, nor_5_out, nor_6_out,
       not_1_out, not_2_out, not_3_out, not_4_out, not_5_out, not_6_out, not_7_out, not_8_out, not_9_out,
       not_10_out, not_11_out, not_12_out, not_13_out, not_14_out, not_15_out, not_16_out, not_17_out,
       not_18_out, not_19_out, not_20_out, not_21_out, not_22_out, not_23_out, not_24_out, not_25_out,
       not_26_out, not_27_out, not_28_out, not_29_out, not_30_out, not_31_out, not_32_out, or_1_out,
       or_2_out, or_3_out, xor_1_out, xor_2_out, xor_3_out, xor_4_out, xor_5_out;

  not not_1 (not_1_out, D3);
  not not_2 (not_2_out, D1);
  not not_3 (not_3_out, D2);
  not not_4 (not_4_out, D0);
  not not_5 (not_5_out, D1);
  not not_6 (not_6_out, D3);
  not not_7 (not_7_out, D3);
  not not_8 (not_8_out, D2);
  not not_9 (not_9_out, D0);
  not not_10 (not_10_out, D0);
  not not_11 (not_11_out, D3);
  not not_12 (not_12_out, D1);
  not not_13 (not_13_out, D1);
  not not_14 (not_14_out, D0);
  not not_15 (not_15_out, D3);
  not not_16 (not_16_out, D2);
  not not_17 (not_17_out, D1);
  not not_18 (not_18_out, D3);
  not not_19 (not_19_out, D2);
  not not_20 (not_20_out, D3);
  not not_21 (not_21_out, D2);
  not not_22 (not_22_out, D1);
  not not_23 (not_23_out, D3);
  not not_24 (not_24_out, D1);
  not not_25 (not_25_out, D3);
  not not_26 (not_26_out, D2);
  not not_27 (not_27_out, D1);
  not not_28 (not_28_out, D3);
  not not_29 (not_29_out, D1);
  not not_30 (not_30_out, D0);
  xor xor_1 (xor_1_out, D2, D0);
  xor xor_2 (xor_2_out, D2, D1);
  xor xor_3 (xor_3_out, D3, D1);
  xor xor_4 (xor_4_out, D2, D0);
  or or_1 (or_1_out, D1, not_10_out);
  xor xor_5 (xor_5_out, D2, D0);
  not not_31 (not_31_out, D2);
  not not_32 (not_32_out, D0);
  and and_1 (and_1_out, D2, not_13_out, not_14_out);
  and and_2 (and_2_out, not_1_out, xor_1_out, not_2_out);
  and and_3 (and_3_out, D3, xor_2_out, D0);
  and and_4 (and_4_out, not_3_out, not_4_out);
  and and_5 (and_5_out, D0, xor_3_out);
  and and_6 (and_6_out, not_5_out, not_6_out, xor_4_out);
  and and_7 (and_7_out, not_7_out, not_8_out, D1, not_9_out);
  and and_8 (and_8_out, D3, D2, or_1_out);
  and and_9 (and_9_out, xor_5_out, not_11_out, not_12_out);
  and and_10 (and_10_out, D2, D1, D0);
  and and_11 (and_11_out, D3, not_31_out, D1, not_32_out);
  or or_2 (or_2_out, and_1_out, D0);
  and and_12 (and_12_out, or_2_out, not_15_out);
  and and_13 (and_13_out, D3, not_16_out, not_17_out, D0);
  and and_14 (and_14_out, not_18_out, not_19_out, D1);
  and and_15 (and_15_out, not_20_out, not_21_out, not_22_out, D0);
  and and_16 (and_16_out, not_23_out, D2, D1, D0);
  and and_17 (and_17_out, D3, D2, not_24_out, D0);
  and and_18 (and_18_out, not_25_out, not_26_out, not_27_out);
  and and_19 (and_19_out, not_28_out, D2, D1, D0);
  and and_20 (and_20_out, D3, D2, not_29_out, not_30_out);
  nor nor_1 (nor_1_out, and_2_out, and_3_out);
  or or_3 (or_3_out, and_4_out, and_5_out, and_6_out);
  nor nor_2 (nor_2_out, and_7_out, and_8_out);
  nor nor_3 (nor_3_out, and_9_out, and_10_out, and_11_out);
  nor nor_4 (nor_4_out, and_12_out, and_13_out);
  nor nor_5 (nor_5_out, and_14_out, and_15_out, and_16_out, and_17_out);
  nor nor_6 (nor_6_out, and_18_out, and_19_out, and_20_out);
  _7_Segment_Display u_7_segment_display_1 (
    .g(nor_6_out), .f(nor_5_out), .a(nor_1_out), .b(or_3_out), .e(nor_4_out), .d(nor_3_out), .c(nor_2_out),
    .dp(Point));
  and and_21 (A, nor_1_out, EN);
  and and_22 (B, or_3_out, EN);
  and and_23 (C, nor_2_out, EN);
  and and_24 (D, nor_3_out, EN);
  and and_25 (E, nor_4_out, EN);
  and and_26 (F, nor_5_out, EN);
  and and_27 (G, nor_6_out, EN);

  assign P = Point;
endmodule

module encoder_4_2 (
  input  A3,
  input  A2,
  input  A1,
  input  A0,
  input  EN,
  output Y1,
  output Y0
);

  wire or_1_out, or_2_out;

  or or_1 (or_1_out, A3, A2);
  or or_2 (or_2_out, A3, A1);
  and and_1 (Y1, or_1_out, EN);
  and and_2 (Y0, or_2_out, EN);
endmodule

module encoder_16_4 (
  input  A15,
  input  A14,
  input  A13,
  input  A12,
  input  A11,
  input  A10,
  input  A9,
  input  A8,
  input  A7,
  input  A6,
  input  A5,
  input  A4,
  input  A3,
  input  A2,
  input  A1,
  input  A0,
  input  EN,
  output Y3,
  output Y2,
  output Y1,
  output Y0
);

  wire or_1_out, or_2_out, or_3_out, or_4_out;

  or or_1 (or_1_out, A15, A14, A12, A11, A10, A13, A9, A8);
  or or_2 (or_2_out, A15, A14, A13, A12, A7, A6, A5, A4);
  or or_3 (or_3_out, A15, A14, A11, A10, A7, A6, A3, A2);
  or or_4 (or_4_out, A15, A13, A11, A9, A7, A5, A3, A1);
  and and_1 (Y3, or_1_out, EN);
  and and_2 (Y2, or_2_out, EN);
  and and_3 (Y1, or_3_out, EN);
  and and_4 (Y0, or_4_out, EN);
endmodule

module priority_encoder_4_2 (
  input  A3,
  input  A2,
  input  A1,
  input  A0,
  input  EN,
  output Y1,
  output Y0
);

  wire and_1_out, not_1_out, or_1_out, or_2_out;

  not not_1 (not_1_out, A2);
  or or_1 (or_1_out, A3, A2);
  or or_2 (or_2_out, A3, and_1_out);
  and and_1 (and_1_out, not_1_out, A1);
  and and_2 (Y1, or_1_out, EN);
  and and_3 (Y0, or_2_out, EN);
endmodule

module priority_encoder_16_4 (
  input  A15,
  input  A14,
  input  A13,
  input  A12,
  input  A11,
  input  A10,
  input  A9,
  input  A8,
  input  A7,
  input  A6,
  input  A5,
  input  A4,
  input  A3,
  input  A2,
  input  A1,
  input  A0,
  input  EN,
  output Y3,
  output Y2,
  output Y1,
  output Y0
);

  wire and_1_out, and_2_out, not_1_out, not_2_out, not_3_out, or_1_out, or_2_out, priority_encoder_4_2_1_y0,
       priority_encoder_4_2_1_y1, priority_encoder_4_2_2_y0, priority_encoder_4_2_2_y1,
       priority_encoder_4_2_3_y0, priority_encoder_4_2_3_y1, priority_encoder_4_2_4_y0,
       priority_encoder_4_2_4_y1, priority_encoder_4_2_5_y0, priority_encoder_4_2_5_y1, V0_out, V1_out,
       V2_out, V3_out;

  or V3 (V3_out, A15, A14, A13, A12);
  or V2 (V2_out, A11, A10, A9, A8);
  or V1 (V1_out, A7, A6, A5, A4);
  or V0 (V0_out, A3, A2, A1, A0);
  not not_1 (not_1_out, V3_out);
  not not_2 (not_2_out, V2_out);
  not not_3 (not_3_out, V1_out);
  and and_1 (and_1_out, not_1_out, not_2_out);
  and and_2 (and_2_out, not_1_out, not_2_out, not_3_out);
  priority_encoder_4_2 priority_encoder_4_2_1 (
    .A3(A15), .A2(A14), .A1(A13), .A0(A12), .EN(EN), .Y1(priority_encoder_4_2_1_y1),
    .Y0(priority_encoder_4_2_1_y0));
  priority_encoder_4_2 priority_encoder_4_2_2 (
    .A3(A11), .A2(A10), .A1(A9), .A0(A8), .EN(not_1_out), .Y1(priority_encoder_4_2_2_y1),
    .Y0(priority_encoder_4_2_2_y0));
  priority_encoder_4_2 priority_encoder_4_2_3 (
    .A3(A7), .A2(A6), .A1(A5), .A0(A4), .EN(and_1_out), .Y1(priority_encoder_4_2_3_y1),
    .Y0(priority_encoder_4_2_3_y0));
  priority_encoder_4_2 priority_encoder_4_2_4 (
    .A3(A3), .A2(A2), .A1(A1), .A0(A0), .EN(and_2_out), .Y1(priority_encoder_4_2_4_y1),
    .Y0(priority_encoder_4_2_4_y0));
  priority_encoder_4_2 priority_encoder_4_2_5 (
    .A3(V3_out), .A2(V2_out), .A1(V1_out), .A0(V0_out), .EN(EN), .Y1(priority_encoder_4_2_5_y1),
    .Y0(priority_encoder_4_2_5_y0));
  or or_1 (or_1_out, priority_encoder_4_2_1_y1, priority_encoder_4_2_2_y1, priority_encoder_4_2_3_y1, priority_encoder_4_2_4_y1);
  or or_2 (or_2_out, priority_encoder_4_2_1_y0, priority_encoder_4_2_2_y0, priority_encoder_4_2_3_y0, priority_encoder_4_2_4_y0);
  and and_3 (Y3, priority_encoder_4_2_5_y1, EN);
  and and_4 (Y2, priority_encoder_4_2_5_y0, EN);
  and and_5 (Y1, or_1_out, EN);
  and and_6 (Y0, or_2_out, EN);
endmodule
