// Logisim project mux.circ as structural Verilog: 10 circuits, main circuit main
module main (
  input  S,
  input  D3,
  input  D2,
  input  D1,
  input  D0,
  input  in_6
);

  wire bcd7seg_1_a, bcd7seg_1_b, bcd7seg_1_c, bcd7seg_1_d, bcd7seg_1_e, bcd7seg_1_f, bcd7seg_1_g,
       bcd7seg_1_p, hex7seg_1_a, hex7seg_1_b, hex7seg_1_c, hex7seg_1_d, hex7seg_1_e, hex7seg_1_f,
       hex7seg_1_g, hex7seg_1_p, mux_8_2_1_1_y0, mux_8_2_1_1_y1, mux_8_2_1_1_y2, mux_8_2_1_1_y3,
       mux_8_2_1_1_y4, mux_8_2_1_1_y5, mux_8_2_1_1_y6, mux_8_2_1_1_y7;

  bcd7seg bcd7seg_1 (
    .D3(D3), .D2(D2), .D1(D1), .D0(D0), .EN(in_6), .A(bcd7seg_1_a), .B(bcd7seg_1_b), .C(bcd7seg_1_c),
    .D(bcd7seg_1_d), .E(bcd7seg_1_e), .F(bcd7seg_1_f), .G(bcd7seg_1_g), .P(bcd7seg_1_p));  // open: Point
  hex7seg hex7seg_1 (
    .D3(D3), .D2(D2), .D1(D1), .D0(D0), .EN(in_6), .A(hex7seg_1_a), .B(hex7seg_1_b), .C(hex7seg_1_c),
    .D(hex7seg_1_d), .E(hex7seg_1_e), .F(hex7seg_1_f), .G(hex7seg_1_g), .P(hex7seg_1_p));  // open: Point
  mux_8_2_1 mux_8_2_1_1 (
    .S0(S), .D00(bcd7seg_1_a), .D01(hex7seg_1_a), .D10(bcd7seg_1_b), .D11(hex7seg_1_b), .D20(bcd7seg_1_c),
    .D21(hex7seg_1_c), .D30(bcd7seg_1_d), .D31(hex7seg_1_d), .D40(bcd7seg_1_e), .D41(hex7seg_1_e),
    .D50(bcd7seg_1_f), .D51(hex7seg_1_f), .D60(bcd7seg_1_g), .D61(hex7seg_1_g), .D70(bcd7seg_1_p),
    .D71(hex7seg_1_p), .Y0(mux_8_2_1_1_y0), .Y1(mux_8_2_1_1_y1), .Y2(mux_8_2_1_1_y2), .Y3(mux_8_2_1_1_y3),
    .Y4(mux_8_2_1_1_y4), .Y5(mux_8_2_1_1_y5), .Y6(mux_8_2_1_1_y6), .Y7(mux_8_2_1_1_y7));
  _7_Segment_Display u_7_segment_display_1 (
    .g(mux_8_2_1_1_y6), .f(mux_8_2_1_1_y5), .a(mux_8_2_1_1_y0), .b(mux_8_2_1_1_y1), .e(mux_8_2_1_1_y4),
    .d(mux_8_2_1_1_y3), .c(mux_8_2_1_1_y2), .dp(mux_8_2_1_1_y7));
endmodule

module decoder_2_4 (
  input  A0,
  input  A1,
  input  EN,
  output Y0,
  output Y1,
  output Y2,
  output Y3
);

  wire not_1_out, not_2_out;

  not not_1 (not_1_out, A1);
  not not_2 (not_2_out, A0);
  and and_1 (Y0, not_2_out, EN, not_1_out);
  and and_2 (Y1, A0, EN, not_1_out);
  and and_3 (Y2, not_2_out, EN, A1);
  and and_4 (Y3, A0, EN, A1);
endmodule

module decoder_1_2 (
  input  A0,
  output Y0,
  output Y1
);

  not not_1 (Y0, A0);

  assign Y1 = A0;
endmodule

module mux_2_1 (
  input  S,
  input  D0,
  input  D1,
  output out_4
);

  wire and_1_out, and_2_out, decoder_1_2_1_y0, decoder_1_2_1_y1;

  decoder_1_2 decoder_1_2_1 (.A0(S), .Y1(decoder_1_2_1_y1), .Y0(decoder_1_2_1_y0));
  and and_1 (and_1_out, D0, decoder_1_2_1_y0);
  and and_2 (and_2_out, decoder_1_2_1_y1, D1);
  or or_1 (out_4, and_1_out, and_2_out);
endmodule

module mux_4_1 (
  input  S1,
  input  S0,
  input  EN,
  input  D0,
  input  D1,
  input  D2,
  input  D3,
  output out_8
);

  wire and_1_out, and_2_out, and_3_out, and_4_out, decoder_2_4_1_y0, decoder_2_4_1_y1, decoder_2_4_1_y2,
       decoder_2_4_1_y3;

  decoder_2_4 decoder_2_4_1 (
    .A0(S0), .A1(S1), .EN(EN), .Y0(decoder_2_4_1_y0), .Y1(decoder_2_4_1_y1), .Y2(decoder_2_4_1_y2),
    .Y3(decoder_2_4_1_y3));
  and and_1 (and_1_out, D0, decoder_2_4_1_y0);
  and and_2 (and_2_out, D1, decoder_2_4_1_y1);
  and and_3 (and_3_out, D2, decoder_2_4_1_y2);
  and and_4 (and_4_out, D3, decoder_2_4_1_y3);
  or or_1 (out_8, and_1_out, and_2_out, and_3_out, and_4_out);
endmodule

module mux_3_4_1 (
  input  S1,
  input  S0,
  input  EN,
  input  D00,
  input  D01,
  input  D02,
  input  D03,
  input  D10,
  input  D11,
  input  D12,
  input  D13,
  input  D20,
  input  D21,
  input  D22,
  input  D23,
  output Y0,
  output Y1,
  output Y2
);

  wire and_1_out, and_2_out, and_3_out, and_4_out, and_5_out, and_6_out, and_7_out, and_8_out, and_9_out,
       and_10_out, and_11_out, and_12_out, decoder_2_4_1_y0, decoder_2_4_1_y1, decoder_2_4_1_y2,
       decoder_2_4_1_y3;

  decoder_2_4 decoder_2_4_1 (
    .A0(S0), .A1(S1), .EN(EN), .Y0(decoder_2_4_1_y0), .Y1(decoder_2_4_1_y1), .Y2(decoder_2_4_1_y2),
    .Y3(decoder_2_4_1_y3));
  and and_1 (and_1_out, D00, decoder_2_4_1_y0);
  and and_2 (and_2_out, D01, decoder_2_4_1_y1);
  and and_3 (and_3_out, D02, decoder_2_4_1_y2);
  and and_4 (and_4_out, D03, decoder_2_4_1_y3);
  and and_5 (and_5_out, D10, decoder_2_4_1_y0);
  and and_6 (and_6_out, D11, decoder_2_4_1_y1);
  and and_7 (and_7_out, D12, decoder_2_4_1_y2);
  and and_8 (and_8_out, D13, decoder_2_4_1_y3);
  and and_9 (and_9_out, D20, decoder_2_4_1_y0);
  and and_10 (and_10_out, D21, decoder_2_4_1_y1);
  and and_11 (and_11_out, D22, decoder_2_4_1_y2);
  and and_12 (and_12_out, D23, decoder_2_4_1_y3);
  or or_1 (Y0, and_1_out, and_2_out, and_3_out, and_4_out);
  or or_2 (Y1, and_5_out, and_6_out, and_7_out, and_8_out);
  or or_3 (Y2, and_9_out, and_10_out, and_11_out, and_12_out);
endmodule

module mux_3_4_1based_on4_1 (
  input  S0,
  input  S1,
  input  D00,
  input  D01,
  input  D02,
  input  D03,
  input  D10,
  input  D11,
  input  D12,
  input  D13,
  input  D20,
  input  D21,
  input  D22,
  input  D23,
  input  EN,
  output Y0,
  output Y1,
  output Y2
);

  mux_4_1 mux_4_1_1 (.S1(S1), .S0(S0), .EN(EN), .D0(D00), .D1(D01), .D2(D02), .D3(D03), .out_8(Y0));
  mux_4_1 mux_4_1_2 (.S1(S1), .S0(S0), .EN(EN), .D0(D10), .D1(D11), .D2(D12), .D3(D13), .out_8(Y1));
  mux_4_1 mux_4_1_3 (.S1(S1), .S0(S0), .EN(EN), .D0(D20), .D1(D21), .D2(D22), .D3(D23), .out_8(Y2));
endmodule

module hex7seg (
  input  D3,
  input  D2,
  input  D1,
  input  D0,
  input  Point,
  input  EN,
  output A,
  output B,
  output C,
  output D,
  output E,
  output F,
  output G,
  output P
);

  wire and_1_out, and_2_out, and_3_out, and_4_out, and_5_out, and_6_out, and_7_out, and_8_out, and_9_out,
       and_10_out, and_11_out, and_12_out, and_13_out, and_14_out, and_15_out, and_16_out, and_17_out,
       and_18_out, and_19_out, and_20_out, nor_1_out, nor_2_out, nor_3_out, nor_4_out, nor_5_out, nor_6_out,
       not_1_out, not_2_out, not_3_out, not_4_out, not_5_out, not_6_out, not_7_out, not_8_out, not_9_out,
       not_10_out, not_11_out, not_12_out, not_13_out, not_14_out, not_15_out, not_16_out, not_17_out,
       not_18_out, not_19_out, not_20_out, not_21_out, not_22_out, not_23_out, not_24_out, not_25_out,
       not_26_out, not_27_out, not_28_out, not_29_out, not_30_out, not_31_out, not_32_out, or_1_out,
       or_2_out, or_3_out, xor_1_out, xor_2_out, xor_3_out, xor_4_out, xor_5_out;

  not not_1 (not_1_out, D3);
  not not_2 (not_2_out, D1);
  not not_3 (not_3_out, D2);
  not not_4 (not_4_out, D0);
  not not_5 (not_5_out, D1);
  not not_6 (not_6_out, D3);
  not not_7 (not_7_out, D3);
  not not_8 (not_8_out, D2);
  not not_9 (not_9_out, D0);
  not not_10 (not_10_out, D0);
  not not_11 (not_11_out, D3);
  not not_12 (not_12_out, D1);
  not not_13 (not_13_out, D1);
  not not_14 (not_14_out, D0);
  not not_15 (not_15_out, D3);
  not not_16 (not_16_out, D2);
  not not_17 (not_17_out, D1);
  not not_18 (not_18_out, D3);
  not not_19 (not_19_out, D2);
  not not_20 (not_20_out, D3);
  not not_21 (not_21_out, D2);
  not not_22 (not_22_out, D1);
  not not_23 (not_23_out, D3);
  not not_24 (not_24_out, D1);
  not not_25 (not_25_out, D3);
  not not_26 (not_26_out, D2);
  not not_27 (not_27_out, D1);
  not not_28 (not_28_out, D3);
  not not_29 (not_29_out, D1);
  not not_30 (not_30_out, D0);
  xor xor_1 (xor_1_out, D2, D0);
  xor xor_2 (xor_2_out, D2, D1);
  xor xor_3 (xor_3_out, D3, D1);
  xor xor_4 (xor_4_out, D2, D0);
  or or_1 (or_1_out, D1, not_10_out);
  xor xor_5 (xor_5_out, D2, D0);
  not not_31 (not_31_out, D2);
  not not_32 (not_32_out, D0);
  and and_1 (and_1_out, D2, not_13_out, not_14_out);
  and and_2 (and_2_out, not_1_out, xor_1_out, not_2_out);
  and and_3 (and_3_out, D3, xor_2_out, D0);
  and and_4 (and_4_out, not_3_out, not_4_out);
  and and_5 (and_5_out, D0, xor_3_out);
  and and_6 (and_6_out, not_5_out, not_6_out, xor_4_out);
  and and_7 (and_7_out, not_7_out, not_8_out, D1, not_9_out);
  and and_8 (and_8_out, D3, D2, or_1_out);
  and and_9 (and_9_out, xor_5_out, not_11_out, not_12_out);
  and and_10 (and_10_out, D2, D1, D0);
  and and_11 (and_11_out, D3, not_31_out, D1, not_32_out);
  or or_2 (or_2_out, and_1_out, D0);
  and and_12 (and_12_out, or_2_out, not_15_out);
  and and_13 (and_13_out, D3, not_16_out, not_17_out, D0);
  and and_14 (and_14_out, not_18_out, not_19_out, D1);
  and and_15 (and_15_out, not_20_out, not_21_out, not_22_out, D0);
  and and_16 (and_16_out, not_23_out, D2, D1, D0);
  and and_17 (and_17_out, D3, D2, not_24_out, D0);
  and and_18 (and_18_out, not_25_out, not_26_out, not_27_out);
  and and_19 (and_19_out, not_28_out, D2, D1, D0);
  and and_20 (and_20_out, D3, D2, not_29_out, not_30_out);
  nor nor_1 (nor_1_out, and_2_out, and_3_out);
  or or_3 (or_3_out, and_4_out, and_5_out, and_6_out);
  nor nor_2 (nor_2_out, and_7_out, and_8_out);
  nor nor_3 (nor_3_out, and_9_out, and_10_out, and_11_out);
  nor nor_4 (nor_4_out, and_12_out, and_13_out);
  nor nor_5 (nor_5_out, and_14_out, and_15_out, and_16_out, and_17_out);
  nor nor_6 (nor_6_out, and_18_out, and_19_out, and_20_out);
  _7_Segment_Display u_7_segment_display_1 (
    .g(nor_6_out), .f(nor_5_out), .a(nor_1_out), .b(or_3_out), .e(nor_4_out), .d(nor_3_out), .c(nor_2_out),
    .dp(Point));
  and and_21 (A, nor_1_out, EN);
  and and_22 (B, or_3_out, EN);
  and and_23 (C, nor_2_out, EN);
  and and_24 (D, nor_3_out, EN);
  and and_25 (E, nor_4_out, EN);
  and and_26 (F, nor_5_out, EN);
  and and_27 (G, nor_6_out, EN);

  assign P = Point;
endmodule

module bcd7seg (
  input  D3,
  input  D2,
  input  D1,
  input  D0,
  input  EN,
  input  Point,
  output A,
  output B,
  output C,
  output D,
  output E,
  output F,
  output G,
  output P
);

  wire and_1_out, and_2_out, and_3_out, and_4_out, and_5_out, and_6_out, and_7_out, and_8_out, and_9_out,
       and_10_out, and_11_out, and_12_out, and_13_out, and_14_out, and_15_out, and_16_out, not_1_out,
       not_2_out, not_3_out, or_1_out, or_2_out, or_3_out, or_4_out, or_5_out, or_6_out, or_7_out;

  not not_1 (not_1_out, D2);
  not not_2 (not_2_out, D1);
  not not_3 (not_3_out, D0);
  and and_1 (and_1_out, D2, D0);
  and and_2 (and_2_out, not_1_out, not_3_out);
  and and_3 (and_3_out, D1, D0);
  and and_4 (and_4_out, not_2_out, not_3_out);
  and and_5 (and_5_out, D1, not_3_out);
  and and_6 (and_6_out, D1, not_1_out);
  and and_7 (and_7_out, not_1_out, not_3_out);
  and and_8 (and_8_out, D2, not_2_out, D0);
  and and_9 (and_9_out, D1, not_3_out);
  and and_10 (and_10_out, not_1_out, not_3_out);
  and and_11 (and_11_out, D2, not_3_out);
  and and_12 (and_12_out, D2, not_2_out);
  and and_13 (and_13_out, not_2_out, not_3_out);
  and and_14 (and_14_out, D1, not_3_out);
  and and_15 (and_15_out, D1, not_1_out);
  and and_16 (and_16_out, D2, not_2_out);
  or or_1 (or_1_out, and_1_out, D3, D1, and_2_out);
  or or_2 (or_2_out, and_3_out, not_1_out, and_4_out);
  or or_3 (or_3_out, D2, not_2_out, D0);
  or or_4 (or_4_out, and_5_out, and_6_out, D3, and_7_out, and_8_out);
  or or_5 (or_5_out, and_9_out, and_10_out);
  or or_6 (or_6_out, D3, and_11_out, and_12_out, and_13_out);
  or or_7 (or_7_out, D3, and_14_out, and_15_out, and_16_out);
  _7_Segment_Display u_7_segment_display_1 (
    .g(or_7_out), .f(or_6_out), .a(or_1_out), .b(or_2_out), .e(or_5_out), .d(or_4_out), .c(or_3_out),
    .dp(Point));
  and and_17 (A, or_1_out, EN);
  and and_18 (B, or_2_out, EN);
  and and_19 (C, or_3_out, EN);
  and and_20 (D, or_4_out, EN);
  and and_21 (E, or_5_out, EN);
  and and_22 (F, or_6_out, EN);
  and and_23 (G, or_7_out, EN);

  assign P = Point;
endmodule

module mux_8_2_1 (
  input  S0,
  input  D00,
  input  D01,
  input  D10,
  input  D11,
  input  D20,
  input  D21,
  input  D30,
  input  D31,
  input  D40,
  input  D41,
  input  D50,
  input  D51,
  input  D60,
  input  D61,
  input  D70,
  input  D71,
  output Y0,
  output Y1,
  output Y2,
  output Y3,
  output Y4,
  output Y5,
  output Y6,
  output Y7
);

  wire and_1_out, and_2_out, and_3_out, and_4_out, and_5_out, and_6_out, and_7_out, and_8_out, and_9_out,
       and_10_out, and_11_out, and_12_out, and_13_out, and_14_out, and_15_out, and_16_out, decoder_1_2_1_y0,
       decoder_1_2_1_y1;

  decoder_1_2 decoder_1_2_1 (.A0(S0), .Y1(decoder_1_2_1_y1), .Y0(decoder_1_2_1_y0));
  and and_1 (and_1_out, D00, decoder_1_2_1_y0);
  and and_2 (and_2_out, D01, decoder_1_2_1_y1);
  and and_3 (and_3_out, D10, decoder_1_2_1_y0);
  and and_4 (and_4_out, D11, decoder_1_2_1_y1);
  and and_5 (and_5_out, D20, decoder_1_2_1_y0);
  and and_6 (and_6_out, D21, decoder_1_2_1_y1);
  and and_7 (and_7_out, D30, decoder_1_2_1_y0);
  and and_8 (and_8_out, D31, decoder_1_2_1_y1);
  and and_9 (and_9_out, D40, decoder_1_2_1_y0);
  and and_10 (and_10_out, D41, decoder_1_2_1_y1);
  and and_11 (and_11_out, D50, decoder_1_2_1_y0);
  and and_12 (and_12_out, D51, decoder_1_2_1_y1);
  and and_13 (and_13_out, D60, decoder_1_2_1_y0);
  and and_14 (and_14_out, D61, decoder_1_2_1_y1);
  and and_15 (and_15_out, D70, decoder_1_2_1_y0);
  and and_16 (and_16_out, D71, decoder_1_2_1_y1);
  or or_1 (Y0, and_1_out, and_2_out);
  or or_2 (Y1, and_3_out, and_4_out);
  or or_3 (Y2, and_5_out, and_6_out);
  or or_4 (Y3, and_7_out, and_8_out);
  or or_5 (Y4, and_9_out, and_10_out);
  or or_6 (Y5, and_11_out, and_12_out);
  or or_7 (Y6, and_13_out, and_14_out);
  or or_8 (Y7, and_15_out, and_16_out);
endmodule
