// Logisim project seq_application.circ as structural Verilog
module d_latch (
  input  RST,
  input  WE,
  input  D,
  output Q,
  output out_5
);

  wire and_1_out, and_2_out, and_3_out, not_1_out, not_2_out, or_1_out;

  not not_1 (not_1_out, D);
  and and_1 (and_1_out, not_1_out, WE);
  and and_2 (and_2_out, WE, D);
  or or_1 (or_1_out, RST, and_1_out);
  not not_2 (not_2_out, RST);
  and and_3 (and_3_out, not_2_out, and_2_out);
  nor nor_1 (Q, or_1_out, out_5);
  nor nor_2 (out_5, Q, and_3_out);
endmodule

module ms_dff (
  input  WE,
  input  RST,
  input  clk,
  input  D,
  output Q
);

  wire and_1_out, and_2_out, d_latch_2_q, not_1_out, or_1_out;

  not not_1 (not_1_out, WE);
  and and_1 (and_1_out, D, WE);
  and and_2 (and_2_out, not_1_out, Q);
  or or_1 (or_1_out, and_1_out, and_2_out);
  d_latch d_latch_1 (.RST(RST), .WE(clk), .D(d_latch_2_q), .Q(Q));  // open: out_5
  d_latch d_latch_2 (.RST(RST), .WE(clk), .D(or_1_out), .Q(d_latch_2_q));  // open: out_5
endmodule

module mb_dff (
  input  WE,
  input  RST,
  input  clk,
  input  D,
  output Q,
  output out_6
);

  wire and_1_out, and_2_out, and_3_out, G_out, nand_1_out, nand_2_out, nand_3_out, not_1_out, not_2_out,
       or_1_out, or_2_out;

  not not_1 (not_1_out, WE);
  and and_1 (and_1_out, D, WE);
  or or_1 (or_1_out, and_1_out, and_2_out);
  and and_2 (and_2_out, not_1_out, Q);
  nand nand_1 (nand_1_out, nand_3_out, nand_2_out);
  nand nand_2 (nand_2_out, nand_1_out, clk);
  nand G (G_out, nand_2_out, clk, nand_3_out);
  nand nand_3 (nand_3_out, G_out, or_1_out);
  not not_2 (not_2_out, RST);
  or or_2 (or_2_out, RST, nand_2_out);
  and and_3 (and_3_out, not_2_out, G_out);
  nand nand_4 (Q, or_2_out, out_6);
  nand nand_5 (out_6, Q, and_3_out);
endmodule

module register4bit (
  input  WE,
  input  clk,
  input  RST,
  input  [3:0] D,
  output [3:0] out_5
);

  mb_dff mb_dff_1 (.WE(WE), .RST(RST), .clk(clk), .D(D[0]), .Q(out_5[0]));  // open: out_6
  mb_dff mb_dff_2 (.WE(WE), .RST(RST), .clk(clk), .D(D[1]), .Q(out_5[1]));  // open: out_6
  mb_dff mb_dff_3 (.WE(WE), .RST(RST), .clk(clk), .D(D[2]), .Q(out_5[2]));  // open: out_6
  mb_dff mb_dff_4 (.WE(WE), .RST(RST), .clk(clk), .D(D[3]), .Q(out_5[3]));  // open: out_6
endmodule

module full_adder (
  input  A,
  input  B,
  input  Cin,
  output S,
  output Cout
);

  wire and_1_out, and_2_out, and_3_out;

  and and_1 (and_1_out, A, B);
  and and_2 (and_2_out, B, Cin);
  and and_3 (and_3_out, A, Cin);
  xor xor_1 (S, A, B, Cin);
  or or_1 (Cout, and_1_out, and_2_out, and_3_out);
endmodule

module adder4bit (
  input  [3:0] A,
  input  [3:0] B,
  input  C,
  output [3:0] out_4
);

  wire full_adder_1_cout, full_adder_2_cout, full_adder_3_cout, full_adder_4_cout;

  full_adder full_adder_1 (.A(A[0]), .B(B[0]), .Cin(C), .S(out_4[0]), .Cout(full_adder_1_cout));
  full_adder full_adder_2 (.A(A[1]), .B(B[1]), .Cin(full_adder_1_cout), .S(out_4[1]), .Cout(full_adder_2_cout));
  full_adder full_adder_3 (.A(A[2]), .B(B[2]), .Cin(full_adder_2_cout), .S(out_4[2]), .Cout(full_adder_3_cout));
  full_adder full_adder_4 (.A(A[3]), .B(B[3]), .Cin(full_adder_3_cout), .S(out_4[3]), .Cout(full_adder_4_cout));
  LED led_1 (.in(full_adder_4_cout));
endmodule

module counter4bit (
  input  [3:0] in_1,
  input  in_2,
  input  in_3,
  output [3:0] out_4
);

  wire clock_1_out;
  wire [3:0] adder4bit_1_out_4;

  Clock clock_1 (.out(clock_1_out));
  adder4bit adder4bit_1 (.A(in_1), .B(out_4), .out_4(adder4bit_1_out_4));  // open: C
  register4bit register4bit_1 (.WE(in_2), .clk(clock_1_out), .RST(in_3), .D(adder4bit_1_out_4), .out_5(out_4));

  // Notes on the sheet:
  //   in_1: initial=0x1
endmodule

module register8bit (
  input  EN,
  input  clk,
  input  RST,
  input  [7:0] D,
  output [7:0] Q
);

  mb_dff mb_dff_1 (.WE(EN), .RST(RST), .clk(clk), .D(D[0]), .Q(Q[0]));  // open: out_6
  mb_dff mb_dff_2 (.WE(EN), .RST(RST), .clk(clk), .D(D[1]), .Q(Q[1]));  // open: out_6
  mb_dff mb_dff_3 (.WE(EN), .RST(RST), .clk(clk), .D(D[2]), .Q(Q[2]));  // open: out_6
  mb_dff mb_dff_4 (.WE(EN), .RST(RST), .clk(clk), .D(D[3]), .Q(Q[3]));  // open: out_6
  mb_dff mb_dff_5 (.WE(EN), .RST(RST), .clk(clk), .D(D[4]), .Q(Q[4]));  // open: out_6
  mb_dff mb_dff_6 (.WE(EN), .RST(RST), .clk(clk), .D(D[5]), .Q(Q[5]));  // open: out_6
  mb_dff mb_dff_7 (.WE(EN), .RST(RST), .clk(clk), .D(D[6]), .Q(Q[6]));  // open: out_6
  mb_dff mb_dff_8 (.WE(EN), .RST(RST), .clk(clk), .D(D[7]), .Q(Q[7]));  // open: out_6
endmodule

module adder8bit (
  input  [7:0] A,
  input  [7:0] B,
  input  Cin,
  output [7:0] S
);

  wire full_adder_1_cout, full_adder_2_cout, full_adder_3_cout, full_adder_4_cout, full_adder_5_cout,
       full_adder_6_cout, full_adder_7_cout, full_adder_8_cout;

  full_adder full_adder_1 (.A(A[0]), .B(B[0]), .Cin(Cin), .S(S[0]), .Cout(full_adder_1_cout));
  full_adder full_adder_2 (.A(A[1]), .B(B[1]), .Cin(full_adder_1_cout), .S(S[1]), .Cout(full_adder_2_cout));
  full_adder full_adder_3 (.A(A[2]), .B(B[2]), .Cin(full_adder_2_cout), .S(S[2]), .Cout(full_adder_3_cout));
  full_adder full_adder_4 (.A(A[3]), .B(B[3]), .Cin(full_adder_3_cout), .S(S[3]), .Cout(full_adder_4_cout));
  full_adder full_adder_5 (.A(A[4]), .B(B[4]), .Cin(full_adder_4_cout), .S(S[4]), .Cout(full_adder_5_cout));
  full_adder full_adder_6 (.A(A[5]), .B(B[5]), .Cin(full_adder_5_cout), .S(S[5]), .Cout(full_adder_6_cout));
  full_adder full_adder_7 (.A(A[6]), .B(B[6]), .Cin(full_adder_6_cout), .S(S[6]), .Cout(full_adder_7_cout));
  full_adder full_adder_8 (.A(A[7]), .B(B[7]), .Cin(full_adder_7_cout), .S(S[7]), .Cout(full_adder_8_cout));
  LED led_1 (.in(full_adder_8_cout));
endmodule

module sum8bit (
  input  in_1,
  input  [7:0] in_2,
  input  in_3,
  output [7:0] out_4
);

  wire clock_1_out;
  wire [7:0] adder8bit_1_s, adder8bit_2_s, register8bit_2_q;

  Clock clock_1 (.out(clock_1_out));
  adder8bit adder8bit_1 (.A(in_2), .B(register8bit_2_q), .S(adder8bit_1_s));  // open: Cin
  register8bit register8bit_1 (.EN(in_1), .clk(clock_1_out), .RST(in_3), .D(adder8bit_2_s), .Q(out_4));
  register8bit register8bit_2 (.EN(in_1), .clk(clock_1_out), .RST(in_3), .D(adder8bit_1_s), .Q(register8bit_2_q));
  adder8bit adder8bit_2 (.A(out_4), .B(register8bit_2_q), .S(adder8bit_2_s));  // open: Cin

  // Notes on the sheet:
  //   in_2: initial=0x1
endmodule
