// Logisim project sub.circ as structural Verilog
module hs1bit (
  input  A,
  input  B,
  output D,
  output Bout
);

  wire not_1_out;

  not not_1 (not_1_out, A);
  xor xor_1 (D, A, B);
  and and_1 (Bout, not_1_out, B);
endmodule

module fs1bit (
  input  A,
  input  B,
  input  Bin,
  output D,
  output Bout
);

  wire and_1_out, and_2_out, and_3_out, not_1_out;

  not not_1 (not_1_out, A);
  and and_1 (and_1_out, not_1_out, B);
  and and_2 (and_2_out, not_1_out, Bin);
  and and_3 (and_3_out, B, Bin);
  xor xor_1 (D, A, B, Bin);
  or or_1 (Bout, and_1_out, and_2_out, and_3_out);
endmodule

module fs1bit_based_hs (
  input  A,
  input  B,
  input  Bin,
  output D,
  output Bout
);

  wire hs1bit_1_bout, hs1bit_1_d, hs1bit_2_bout;

  hs1bit hs1bit_1 (.A(A), .B(B), .D(hs1bit_1_d), .Bout(hs1bit_1_bout));
  hs1bit hs1bit_2 (.A(hs1bit_1_d), .B(Bin), .D(Bout), .Bout(hs1bit_2_bout));
  or or_1 (D, hs1bit_1_bout, hs1bit_2_bout);
endmodule

module fs4bit (
  input  [3:0] A,
  input  [3:0] B,
  input  Bin,
  output [3:0] out_4
);

  wire fs1bit_1_bout, fs1bit_2_bout, fs1bit_3_bout, fs1bit_4_bout;

  fs1bit fs1bit_1 (.A(A[0]), .B(B[0]), .Bin(Bin), .D(out_4[0]), .Bout(fs1bit_1_bout));
  fs1bit fs1bit_2 (.A(A[1]), .B(B[1]), .Bin(fs1bit_1_bout), .D(out_4[1]), .Bout(fs1bit_2_bout));
  fs1bit fs1bit_3 (.A(A[2]), .B(B[2]), .Bin(fs1bit_2_bout), .D(out_4[2]), .Bout(fs1bit_3_bout));
  fs1bit fs1bit_4 (.A(A[3]), .B(B[3]), .Bin(fs1bit_3_bout), .D(out_4[3]), .Bout(fs1bit_4_bout));
  LED led_1 (.in(fs1bit_4_bout));
endmodule
